// Digital circuit 8Bit RAM.dig as structural Verilog
module _8Bit_RAM (
  input  Addr0,
  input  Addr1,
  input  Addr2,
  input  Addr3,
  input  Addr4,
  input  Addr5,
  input  Addr6,
  input  Addr7,
  input  Data0,
  input  Data1,
  input  Data2,
  input  Data3,
  input  Data4,
  input  Data5,
  input  Data6,
  input  Data7,
  input  Load,
  input  Store,
  input  Clock,
  output DataOut0,
  output DataOut1,
  output DataOut2,
  output DataOut3,
  output DataOut4,
  output DataOut5,
  output DataOut6,
  output DataOut7
);

  wire d_ff_1_q, d_ff_2_q;

  D_FF d_ff_1 (.D(Load), .C(Clock), .Q(d_ff_1_q));  // open: nQ
  RAMDualPort #(.AddrBits(8), .Bits(8)) ramdualport_1 (
    .A({Addr7, Addr6, Addr5, Addr4, Addr3, Addr2, Addr1, Addr0}),
    .Din({Data7, Data6, Data5, Data4, Data3, Data2, Data1, Data0}), .str(Store), .C(Clock), .ld(d_ff_2_q),
    .D({DataOut7, DataOut6, DataOut5, DataOut4, DataOut3, DataOut2, DataOut1, DataOut0}));
  D_FF d_ff_2 (.D(d_ff_1_q), .C(Clock), .Q(d_ff_2_q));  // open: nQ
endmodule
