// Digital circuit 1Bit Logic Operations.dig as structural Verilog
module _1Bit_Logic_Operations (
  input  in_1,
  input  in_2,
  input  in_3,
  input  in_4,
  input  in_5,
  input  in_6,
  output out_7
);

  wire _7404_1_pin2, _7408_1_pin3, _7408_2_pin3, _7408_2_pin6, _7408_2_pin8, _7408_2_pin11, _7432_1_pin3,
       _7432_2_pin3, _7432_2_pin6, _7486_1_pin3;

  _7404 _7404_1 (
    .pin1(in_1), .pin2(_7404_1_pin2), .pin3(1'b0), .pin5(1'b0), .pin7(1'b0), .pin9(1'b0), .pin11(1'b0),
    .pin13(1'b0), .pin14(1'b1));  // open: pin4, pin6, pin8, pin10, pin12
  _7408 _7408_1 (
    .pin1(in_1), .pin2(in_2), .pin3(_7408_1_pin3), .pin4(1'b0), .pin5(1'b0), .pin7(1'b0), .pin9(1'b0),
    .pin10(1'b0), .pin12(1'b0), .pin13(1'b0), .pin14(1'b1));  // open: pin6, pin8, pin11
  _7432 _7432_1 (
    .pin1(in_1), .pin2(in_2), .pin3(_7432_1_pin3), .pin4(1'b0), .pin5(1'b0), .pin7(1'b0), .pin9(1'b0),
    .pin10(1'b0), .pin12(1'b0), .pin13(1'b0), .pin14(1'b1));  // open: pin6, pin8, pin11
  _7486 _7486_1 (
    .pin1(in_1), .pin2(in_2), .pin3(_7486_1_pin3), .pin4(1'b0), .pin5(1'b0), .pin7(1'b0), .pin9(1'b0),
    .pin10(1'b0), .pin12(1'b0), .pin13(1'b0), .pin14(1'b1));  // open: pin6, pin8, pin11
  _7408 _7408_2 (
    .pin1(in_3), .pin2(_7404_1_pin2), .pin3(_7408_2_pin3), .pin4(in_4), .pin5(_7408_1_pin3),
    .pin6(_7408_2_pin6), .pin7(1'b0), .pin8(_7408_2_pin8), .pin9(in_5), .pin10(_7432_1_pin3),
    .pin11(_7408_2_pin11), .pin12(in_6), .pin13(_7486_1_pin3), .pin14(1'b1));
  _7432 _7432_2 (
    .pin1(_7408_2_pin3), .pin2(_7408_2_pin6), .pin3(_7432_2_pin3), .pin4(_7432_2_pin3), .pin5(_7408_2_pin8),
    .pin6(_7432_2_pin6), .pin7(1'b0), .pin8(out_7), .pin9(_7432_2_pin6), .pin10(_7408_2_pin11), .pin12(1'b0),
    .pin13(1'b0), .pin14(1'b1));  // open: pin11
endmodule
