// Digital circuit 8Bit Adder.dig as structural Verilog
module _8Bit_Adder (
  input  [7:0] Input_A,
  input  [7:0] Input_B,
  input  Subtract,
  output [7:0] Result,
  output Carry_Out,
  output Overflow
);

  wire _7483_1_pin14, _7486_1_pin3, _7486_1_pin6, _7486_1_pin8, _7486_1_pin11, _7486_2_pin3, _7486_2_pin6,
       _7486_2_pin8, _7486_2_pin11, _74183_1__1cn_plus_1, _74183_1__2cn_plus_1, _74183_2__1cn_plus_1;

  _7486 _7486_1 (
    .pin1(Input_B[0]), .pin2(Subtract), .pin3(_7486_1_pin3), .pin4(Input_B[1]), .pin5(Subtract),
    .pin6(_7486_1_pin6), .pin7(1'b0), .pin8(_7486_1_pin8), .pin9(Input_B[2]), .pin10(Subtract),
    .pin11(_7486_1_pin11), .pin12(Input_B[3]), .pin13(Subtract), .pin14(1'b1));
  _7486 _7486_2 (
    .pin1(Input_B[4]), .pin2(Subtract), .pin3(_7486_2_pin3), .pin4(Input_B[5]), .pin5(Subtract),
    .pin6(_7486_2_pin6), .pin7(1'b0), .pin8(_7486_2_pin8), .pin9(Input_B[6]), .pin10(Subtract),
    .pin11(_7486_2_pin11), .pin12(Input_B[7]), .pin13(Subtract), .pin14(1'b1));
  _7483 _7483_1 (
    .pin1(Input_A[3]), .pin2(Result[2]), .pin3(Input_A[2]), .pin4(_7486_1_pin8), .pin5(1'b1),
    .pin6(Result[1]), .pin7(_7486_1_pin6), .pin8(Input_A[1]), .pin9(Result[0]), .pin10(Input_A[0]),
    .pin11(_7486_1_pin3), .pin12(1'b0), .pin13(Subtract), .pin14(_7483_1_pin14), .pin15(Result[3]),
    .pin16(_7486_1_pin11));
  _74183 _74183_1 (
    ._2B(_7486_2_pin6), ._2Cn(_74183_1__1cn_plus_1), ._1Z(Result[4]), ._2A(Input_A[5]), ._2Z(Result[5]),
    ._1Cn_plus_1(_74183_1__1cn_plus_1), ._1Cn(_7483_1_pin14), ._1A(Input_A[4]), ._1B(_7486_2_pin3),
    ._2Cn_plus_1(_74183_1__2cn_plus_1), .VCC(1'b1), .GND(1'b0));
  _74183 _74183_2 (
    ._2B(_7486_2_pin11), ._2Cn(_74183_2__1cn_plus_1), ._1Z(Result[6]), ._2A(Input_A[7]), ._2Z(Result[7]),
    ._1Cn_plus_1(_74183_2__1cn_plus_1), ._1Cn(_74183_1__2cn_plus_1), ._1A(Input_A[6]), ._1B(_7486_2_pin8),
    ._2Cn_plus_1(Carry_Out), .VCC(1'b1), .GND(1'b0));
  _7486 _7486_3 (
    .pin1(_74183_2__1cn_plus_1), .pin2(Carry_Out), .pin3(Overflow), .pin4(1'b0), .pin5(1'b0), .pin7(1'b0),
    .pin9(1'b0), .pin10(1'b0), .pin12(1'b0), .pin13(1'b0), .pin14(1'b1));  // open: pin6, pin8, pin11

  // Notes on the sheet:
  //   these different adders were used
  //   to allow for the detection of an
  //   overflow after a subtraction,
  //   as the carry of the previous to
  //   last bit and the last bit are needed
  //   for that
endmodule
