// Digital circuit 8Bit Comparator 2.0 (unused).dig as structural Verilog
module _8Bit_Comparator_2_0__unused (
  input  [7:0] Q,
  input  [7:0] P,
  output P_gt_Q,
  output P_eq_Q,
  output P_lt_Q
);

  wire _7485_1_pin5, _7485_1_pin6, _7485_1_pin7;

  _7485 _7485_1 (
    .pin1(Q[3]), .pin2(1'b0), .pin3(1'b1), .pin4(1'b0), .pin5(_7485_1_pin5), .pin6(_7485_1_pin6),
    .pin7(_7485_1_pin7), .pin8(1'b0), .pin9(Q[0]), .pin10(P[0]), .pin11(Q[1]), .pin12(P[1]), .pin13(P[2]),
    .pin14(Q[2]), .pin15(P[3]), .pin16(1'b1));
  _7485 _7485_2 (
    .pin1(Q[7]), .pin2(_7485_1_pin5), .pin3(_7485_1_pin6), .pin4(_7485_1_pin7), .pin5(P_gt_Q), .pin6(P_eq_Q),
    .pin7(P_lt_Q), .pin8(1'b0), .pin9(Q[4]), .pin10(P[4]), .pin11(Q[5]), .pin12(P[5]), .pin13(P[6]),
    .pin14(Q[6]), .pin15(P[7]), .pin16(1'b1));
  // _74682 _74682_1: pin names not known
endmodule
