// Digital circuit 8Bit Comparator.dig as structural Verilog
module _8Bit_Comparator (
  input  [7:0] in_1,
  input  [7:0] in_3,
  output out_2,
  output out_4
);

  _74682 _74682_1 (
    .pin1(out_2), .pin2(in_3[0]), .pin3(in_1[0]), .pin4(in_3[1]), .pin5(in_1[1]), .pin6(in_3[2]),
    .pin7(in_1[2]), .pin8(in_3[3]), .pin9(in_1[3]), .pin10(1'b0), .pin11(in_3[4]), .pin12(in_1[4]),
    .pin13(in_3[5]), .pin14(in_1[5]), .pin15(in_3[6]), .pin16(in_1[6]), .pin17(in_3[7]), .pin18(in_1[7]),
    .pin19(out_4), .pin20(1'b1));
endmodule
