// Digital circuit 8Bit Shift Register.dig as structural Verilog
module _8Bit_Shift_Register (
  input  [7:0] A,
  input  nR,
  input  [1:0] S0,
  input  CLK,
  input  [1:0] S1,
  output [7:0] Q
);

  // _74194real _74194real_1: pin names not known; wires that end beside it: nR, 1'b0, A[0], A[1], A[2], A[3], Q[4], 1'b0, 1'b1, Q[0], Q[1], Q[2], Q[3], CLK, S1, S0
  // _74194real _74194real_2: pin names not known; wires that end beside it: nR, Q[3], A[4], A[5], A[6], A[7], 1'b0, 1'b0, 1'b1, Q[4], Q[5], Q[6], Q[7], CLK, S1, S0

  // Notes on the sheet:
  //   01 -> SHL (shift left)
  //   10 -> SHR (shift right)
  //   11 -> SLD (shift register load)
endmodule
