// Digital circuit ALU CMD Decoder.dig as structural Verilog
module ALU_CMD_Decoder (
  input  [7:0] CMD,
  output LDA,
  output LDB,
  output ADD,
  output SUB,
  output INC,
  output TOF,
  output CMP,
  output NOT,
  output OR,
  output XOR,
  output AND,
  output SHL,
  output SHR,
  output SLD,
  output LDF,
  output CLA,
  output CLB
);


  // Notes on the sheet:
  //   CMD
  //   00 NOP
  //   01 LDA
  //   02 LDB
  //   03 ADD
  //   04 SUB
  //   05 INC
  //   06 TOF
  //   07 CMP
  //   08 NOT
  //   09 OR
  //   0A XOR
  //   0B AND
  //   0C SHL
  //   0D SHR
  //   0E SLD
  //   0F LDF
  //   .
  //   00000000
  //   00000001
  //   00000010
  //   00000011
  //   00000100
  //   00000101
  //   00000110
  //   00000111
  //   00001000
  //   00001001
  //   00001010
  //   00001011
  //   00001100
  //   00001101
  //   00001110
  //   00001111
  //   000 on the multiplexer should not be connected
  //   Q
  //   00 ->  X
  //   01 -> 10
  //   02 -> 10
  //   03 -> 00
  //   04 -> 10
  //   05 ->
  //   06 ->
  //   07 ->  X
  //   08 -> 00
  //   09 -> 01
  //   0A -> 10
  //   0B -> 11
  //   0C -> 01
  //   0D -> 10
  //   0E -> 11
  //   0F -> 10
  //   possible options:
  //   SN74BCT2424
  //   SN74154
  //   Modules:
  //   -
  //   LD
  //   LD
  //   ADD
  //   ADD
  //   ADD
  //   TOF
  //   CMP
  //   LOGIC
  //   LOGIC
  //   LOGIC
  //   LOGIC
  //   SHIFT
  //   SHIFT
  //   SHIFT
  //   FLAGS
  //   Out:
  //   -> N
  //   -> N
  //   -> N
  //   -> Y
  //   -> Y
  //   -> Y
  //   -> Y
  //   -> N
  //   -> Y
  //   -> Y
  //   -> Y
  //   -> Y
  //   -> Y
  //   -> Y
  //   -> N
  //   -> Y
  //   MUX:
  //   00 -> 000
  //   01 -> 000
  //   02 -> 000
  //   03 -> 001
  //   04 -> 001
  //   05 -> 001
  //   06 -> 010
  //   07 -> 000
  //   08 -> 011
  //   09 -> 011
  //   0A -> 011
  //   0B -> 011
  //   0C -> 100
  //   0D -> 100
  //   0E -> 000
  //   0F -> 101
  //   Description:
  //   no operation
  //   load to register A
  //   load to register B
  //   add
  //   subract
  //   increment
  //   true or false
  //   compare
  //   not
  //   or
  //   exclusive or
  //   and
  //   shift left
  //   shift right
  //   load to shift register
  //   load flags
  //   CLR
endmodule
