// Digital circuit CMD DEC.dig as structural Verilog
module CMD_DEC (
  input  [7:0] CMD_IN,
  input  [7:0] CMD_CMP,
  output CMD_EN
);

  // _74ALS518 _74als518_1: pin names not known; wires that end beside it: 1'b0, CMD_CMP[0], CMD_IN[0], CMD_CMP[1], CMD_IN[1], CMD_CMP[2], CMD_IN[2], CMD_CMP[3], CMD_IN[3], 1'b0, 1'b1, CMD_EN, CMD_IN[7], CMD_CMP[7], CMD_IN[6], CMD_CMP[6], CMD_IN[5], CMD_CMP[5], CMD_IN[4], CMD_CMP[4]
  // Pins of 1 and 8 bits meet at CMD_CMP
  // Pins of 1 and 8 bits meet at CMD_IN

  // Notes on the sheet:
  //   A single 8bit command decoder
  //   should use 74hc688 as it's cheaper
endmodule
