// Digital circuit Flag Register.dig as structural Verilog
module Flag_Register (
  input  gt,
  input  eq,
  input  Co,
  input  C7,
  input  SAF,
  input  [1:0] Adr,
  input  LDF,
  input  SCF,
  output Q
);

  wire _7474_1_pin5, _7474_1_pin9, _7474_2_pin5, _7474_2_pin9;

  _7474 _7474_1 (
    .pin1(1'b1), .pin2(C7), .pin3(SAF), .pin4(1'b1), .pin5(_7474_1_pin5), .pin7(1'b0), .pin9(_7474_1_pin9),
    .pin10(1'b1), .pin11(SAF), .pin12(Co), .pin13(1'b1), .pin14(1'b1));  // open: pin6, pin8
  _7474 _7474_2 (
    .pin1(1'b1), .pin2(gt), .pin3(SCF), .pin4(1'b1), .pin5(_7474_2_pin5), .pin7(1'b0), .pin9(_7474_2_pin9),
    .pin10(1'b1), .pin11(SCF), .pin12(eq), .pin13(1'b1), .pin14(1'b1));  // open: pin6, pin8
  _74153 _74153_1 (
    .pin1(1'b0), .pin2(Adr[1]), .pin3(_7474_2_pin9), .pin4(_7474_2_pin5), .pin5(_7474_1_pin9),
    .pin6(_7474_1_pin5), .pin7(Q), .pin8(1'b0), .pin10(1'b0), .pin11(1'b0), .pin12(1'b0), .pin13(1'b0),
    .pin14(Adr[0]), .pin15(1'b0), .pin16(1'b1));  // open: pin9

  // Notes on the sheet:
  //   Store Addition Flags
  //   Store Comparison Flags
  //   Load Flags
  //   could use the 74279 though it says
  //   it is a nonstable configuration
endmodule
