// Digital circuit 8Bit Graphics Card.dig as structural Verilog
module _8Bit_Graphics_Card (
);

  ROM #(.AddrBits(8), .Bits(64)) Sprites_Low_Byte ();  // open: A, sel, D
  ROM #(.AddrBits(8), .Bits(64)) Sprites_High_Byte ();  // open: A, sel, D
  ROM #(.AddrBits(8), .Bits(21)) Sprite_Data ();  // open: A, sel, D
  ROM #(.AddrBits(8), .Bits(64)) Tiles_Low_Byte ();  // open: A, sel, D
  ROM #(.AddrBits(8), .Bits(64)) Tiles_High_Byte ();  // open: A, sel, D
  ROM #(.AddrBits(8)) Tile_Data ();  // open: A, sel, D
  ROM #(.AddrBits(10), .Bits(8)) Background ();  // open: A, sel, D
  ROM Screen_Out ();  // open: A, sel, D
endmodule
