// Digital circuit Division.dig as structural Verilog
module Division (
  input  [7:0] in_1,
  input  [7:0] in_2,
  input  in_3
);

  wire [3:0] and_1_out, monoflop_1_q;

  Monoflop monoflop_1 (.C(in_3), .R(1'b0), .Q(monoflop_1_q[0]));  // open: nQ
  assign and_1_out = 4'b1000 & monoflop_1_q;  // And and_1, 4 bits wide
  BarrelShifter #(.Bits(8)) barrelshifter_1 (.in(in_1), .shift(and_1_out));  // open: out
  // _74194 _74194_1: pin names not known
  // Pins of 1 and 4 bits meet at monoflop_1_q
endmodule
