// Digital circuit 4Bit ALU Command Decoder.dig as structural Verilog
module _4Bit_ALU_Command_Decoder (
  input  Command_Pin1,
  input  Command_Pin2,
  input  Command_Pin3,
  input  Command_Pin4,
  output add,
  output sub,
  output cmp_equ,
  output cmp_big,
  output cmp_sma,
  output \not ,
  output \and ,
  output \or ,
  output \xor 
);

  and and_1 (add, Command_Pin1, ~Command_Pin2, Command_Pin3, ~Command_Pin4);  // And
  and and_2 (sub, ~Command_Pin1, Command_Pin2, Command_Pin3, ~Command_Pin4);  // And
  and and_3 (cmp_equ, Command_Pin1, Command_Pin2, Command_Pin3, ~Command_Pin4);  // And
  and and_4 (cmp_big, ~Command_Pin1, ~Command_Pin2, ~Command_Pin3, Command_Pin4);  // And
  and and_5 (cmp_sma, Command_Pin1, ~Command_Pin2, ~Command_Pin3, Command_Pin4);  // And
  and and_6 (\not , ~Command_Pin1, Command_Pin2, ~Command_Pin3, Command_Pin4);  // And
  and and_7 (\and , Command_Pin1, Command_Pin2, ~Command_Pin3, Command_Pin4);  // And
  and and_8 (\or , ~Command_Pin1, ~Command_Pin2, Command_Pin3, Command_Pin4);  // And
  and and_9 (\xor , Command_Pin1, ~Command_Pin2, Command_Pin3, Command_Pin4);  // And

  // Notes on the sheet:
  //   Command_Pin1: pin 1
  //   Command_Pin2: pin 2
  //   Command_Pin3: pin 3
  //   Command_Pin4: pin 4
  //   add: pin 5
  //   sub: pin 6
  //   cmp_equ: pin 7
  //   cmp_big: pin 8
  //   cmp_sma: pin 9
  //   not: pin 10
  //   and: pin 11
  //   or: pin 12
  //   xor: pin 13
endmodule
