// Digital circuit 4Bit Computer Command Decoder.dig as structural Verilog
module _4Bit_Computer_Command_Decoder (
  input  Cmd_Pin0,
  input  Cmd_Pin1,
  input  Cmd_Pin2,
  input  Cmd_Pin3,
  output Write,
  output Load,
  output Jump,
  output Jump_if,
  output Write_num,
  output Halt
);

  and and_1 (Write, Cmd_Pin0, ~Cmd_Pin1, ~Cmd_Pin2, ~Cmd_Pin3);  // And
  and and_2 (Load, ~Cmd_Pin0, Cmd_Pin1, ~Cmd_Pin2, ~Cmd_Pin3);  // And
  and and_3 (Jump, Cmd_Pin0, Cmd_Pin1, ~Cmd_Pin2, ~Cmd_Pin3);  // And
  and and_4 (Jump_if, ~Cmd_Pin0, ~Cmd_Pin1, Cmd_Pin2, ~Cmd_Pin3);  // And
  and and_5 (Write_num, ~Cmd_Pin0, Cmd_Pin1, Cmd_Pin2, Cmd_Pin3);  // And
  and and_6 (Halt, Cmd_Pin0, Cmd_Pin1, Cmd_Pin2, Cmd_Pin3);
endmodule
