// Digital circuit 8Bit ALU.dig as structural Verilog
module _8Bit_ALU (
  input  Num1In_Bit0,
  input  Num1In_Bit1,
  input  Num1In_Bit2,
  input  Num1In_Bit3,
  input  Num1In_Bit4,
  input  Num1In_Bit5,
  input  Num1In_Bit6,
  input  Num1In_Bit7,
  input  Num2In_Bit0,
  input  Num2In_Bit1,
  input  Num2In_Bit2,
  input  Num2In_Bit3,
  input  Num2In_Bit4,
  input  Num2In_Bit5,
  input  Num2In_Bit6,
  input  Num2In_Bit7,
  input  Cmd_Pin0,
  input  Cmd_Pin1,
  input  Cmd_Pin2,
  input  Cmd_Pin3,
  input  CLK,
  output Out_Bit0,
  output Out_Bit1,
  output Out_Bit2,
  output Out_Bit3,
  output Out_Bit4,
  output Out_Bit5,
  output Out_Bit6,
  output Out_Bit7,
  output Overflow
);

  wire _4bit_alu_command_decoder_1_add, _4bit_alu_command_decoder_1_and, _4bit_alu_command_decoder_1_cmp_big,
       _4bit_alu_command_decoder_1_cmp_equ, _4bit_alu_command_decoder_1_cmp_sma,
       _4bit_alu_command_decoder_1_not, _4bit_alu_command_decoder_1_or, _4bit_alu_command_decoder_1_sub,
       _4bit_alu_command_decoder_1_xor, _8bit_adder_1_out0, _8bit_adder_1_out1, _8bit_adder_1_out2,
       _8bit_adder_1_out3, _8bit_adder_1_out4, _8bit_adder_1_out5, _8bit_adder_1_out6, _8bit_adder_1_out7,
       _8bit_adder_1_overflow, _8bit_comparator_1_out, and_1_out, and_2_out, and_3_out, and_4_out, and_5_out,
       and_6_out, and_7_out, and_8_out, and_9_out, and_10_out, and_11_out, and_12_out, and_13_out,
       and_14_out, and_15_out, and_16_out, d_ff_1_q, d_ff_2_q, d_ff_3_q, d_ff_4_q, d_ff_5_q, d_ff_6_q,
       d_ff_7_q, d_ff_8_q, d_ff_9_q, d_ff_10_q, delay_1_out, or_1_out, or_2_out, or_3_out, or_4_out,
       or_5_out, or_6_out, xor_1_out;

  D_FF d_ff_1 (.D(delay_1_out), .C(CLK), .Q(d_ff_1_q));  // open: nQ
  Delay #(.delayTime(3)) delay_1 (.in(or_2_out), .out(delay_1_out));
  _4Bit_ALU_Command_Decoder _4bit_alu_command_decoder_1 (
    .Command_Pin1(Cmd_Pin0), .Command_Pin2(Cmd_Pin1), .Command_Pin3(Cmd_Pin2), .Command_Pin4(Cmd_Pin3),
    .add(_4bit_alu_command_decoder_1_add), .sub(_4bit_alu_command_decoder_1_sub),
    .cmp_equ(_4bit_alu_command_decoder_1_cmp_equ), .cmp_big(_4bit_alu_command_decoder_1_cmp_big),
    .cmp_sma(_4bit_alu_command_decoder_1_cmp_sma), .\not (_4bit_alu_command_decoder_1_not),
    .\and (_4bit_alu_command_decoder_1_and), .\or (_4bit_alu_command_decoder_1_or),
    .\xor (_4bit_alu_command_decoder_1_xor));
  or or_1 (or_1_out, _4bit_alu_command_decoder_1_add, _4bit_alu_command_decoder_1_sub);
  or or_2 (or_2_out, or_1_out, _4bit_alu_command_decoder_1_cmp_equ, _4bit_alu_command_decoder_1_cmp_big, _4bit_alu_command_decoder_1_cmp_sma, _4bit_alu_command_decoder_1_not, _4bit_alu_command_decoder_1_and, _4bit_alu_command_decoder_1_or, _4bit_alu_command_decoder_1_xor);
  or or_3 (or_3_out, Num1In_Bit0, Num1In_Bit1, Num1In_Bit2, Num1In_Bit3, Num1In_Bit4, Num1In_Bit5, Num1In_Bit6, Num1In_Bit7);
  or or_4 (or_4_out, Num2In_Bit0, Num2In_Bit1, Num2In_Bit2, Num2In_Bit3, Num2In_Bit4, Num2In_Bit5, Num2In_Bit6, Num2In_Bit7);
  and and_1 (and_1_out, ~or_3_out, _4bit_alu_command_decoder_1_not);  // And
  and and_2 (and_2_out, or_3_out, _4bit_alu_command_decoder_1_and);
  and and_3 (and_3_out, or_3_out, _4bit_alu_command_decoder_1_or);
  and and_4 (and_4_out, or_3_out, _4bit_alu_command_decoder_1_xor);
  and and_5 (and_5_out, or_4_out, _4bit_alu_command_decoder_1_and);
  and and_6 (and_6_out, or_4_out, _4bit_alu_command_decoder_1_or);
  and and_7 (and_7_out, or_4_out, _4bit_alu_command_decoder_1_xor);
  and and_8 (and_8_out, and_2_out, and_5_out);
  or or_5 (or_5_out, and_3_out, and_6_out);
  xor xor_1 (xor_1_out, and_4_out, and_7_out);
  _8Bit_Adder _8bit_adder_1 (
    .Bit0(Num1In_Bit0), .Bit1(Num1In_Bit1), .Bit2(Num1In_Bit2), .Bit3(Num1In_Bit3), .Bit4(Num1In_Bit4),
    .Bit5(Num1In_Bit5), .Bit6(Num1In_Bit6), .Bit7(Num1In_Bit7), .Bit8(Num2In_Bit0), .Bit9(Num2In_Bit1),
    .Bit10(Num2In_Bit2), .Bit11(Num2In_Bit3), .Bit12(Num2In_Bit4), .Bit13(Num2In_Bit5), .Bit14(Num2In_Bit6),
    .Bit15(Num2In_Bit7), .Add_Sub(_4bit_alu_command_decoder_1_sub), .Out0(_8bit_adder_1_out0),
    .Out1(_8bit_adder_1_out1), .Out2(_8bit_adder_1_out2), .Out3(_8bit_adder_1_out3),
    .Out4(_8bit_adder_1_out4), .Out5(_8bit_adder_1_out5), .Out6(_8bit_adder_1_out6),
    .Out7(_8bit_adder_1_out7), .Overflow(_8bit_adder_1_overflow));
  _8Bit_Comparator _8bit_comparator_1 (
    .Bit0(Num1In_Bit0), .Bit1(Num1In_Bit1), .Bit2(Num1In_Bit2), .Bit3(Num1In_Bit3), .Bit4(Num1In_Bit4),
    .Bit5(Num1In_Bit5), .Bit6(Num1In_Bit6), .Bit7(Num1In_Bit7), .Bit8(Num2In_Bit0), .Bit9(Num2In_Bit1),
    .Bit10(Num2In_Bit2), .Bit11(Num2In_Bit3), .Bit12(Num2In_Bit4), .Bit13(Num2In_Bit5), .Bit14(Num2In_Bit6),
    .Bit15(Num2In_Bit7), .Equal(_4bit_alu_command_decoder_1_cmp_equ),
    .Bigger(_4bit_alu_command_decoder_1_cmp_big), .Smaller(_4bit_alu_command_decoder_1_cmp_sma),
    .Out(_8bit_comparator_1_out));
  or or_6 (or_6_out, and_1_out, and_8_out, or_5_out, xor_1_out, _8bit_comparator_1_out, and_9_out);
  and and_9 (and_9_out, or_1_out, _8bit_adder_1_out0);
  and and_10 (and_10_out, or_1_out, _8bit_adder_1_out1);
  and and_11 (and_11_out, or_1_out, _8bit_adder_1_out2);
  and and_12 (and_12_out, or_1_out, _8bit_adder_1_out3);
  and and_13 (and_13_out, or_1_out, _8bit_adder_1_out4);
  and and_14 (and_14_out, or_1_out, _8bit_adder_1_out5);
  and and_15 (and_15_out, or_1_out, _8bit_adder_1_out6);
  and and_16 (and_16_out, or_1_out, _8bit_adder_1_out7);
  D_FF d_ff_2 (.D(or_6_out), .C(d_ff_1_q), .Q(d_ff_2_q));  // open: nQ
  D_FF d_ff_3 (.D(and_10_out), .C(d_ff_1_q), .Q(d_ff_3_q));  // open: nQ
  D_FF d_ff_4 (.D(and_11_out), .C(d_ff_1_q), .Q(d_ff_4_q));  // open: nQ
  D_FF d_ff_5 (.D(and_12_out), .C(d_ff_1_q), .Q(d_ff_5_q));  // open: nQ
  D_FF d_ff_6 (.D(and_13_out), .C(d_ff_1_q), .Q(d_ff_6_q));  // open: nQ
  D_FF d_ff_7 (.D(and_14_out), .C(d_ff_1_q), .Q(d_ff_7_q));  // open: nQ
  D_FF d_ff_8 (.D(and_15_out), .C(d_ff_1_q), .Q(d_ff_8_q));  // open: nQ
  D_FF d_ff_9 (.D(and_16_out), .C(d_ff_1_q), .Q(d_ff_9_q));  // open: nQ
  D_FF d_ff_10 (.D(_8bit_adder_1_overflow), .C(d_ff_1_q), .Q(d_ff_10_q));  // open: nQ
  and and_17 (Out_Bit0, d_ff_2_q, d_ff_1_q);
  and and_18 (Out_Bit1, d_ff_3_q, d_ff_1_q);
  and and_19 (Out_Bit2, d_ff_4_q, d_ff_1_q);
  and and_20 (Out_Bit3, d_ff_5_q, d_ff_1_q);
  and and_21 (Out_Bit4, d_ff_6_q, d_ff_1_q);
  and and_22 (Out_Bit5, d_ff_7_q, d_ff_1_q);
  and and_23 (Out_Bit6, d_ff_8_q, d_ff_1_q);
  and and_24 (Out_Bit7, d_ff_9_q, d_ff_1_q);
  and and_25 (Overflow, d_ff_10_q, d_ff_1_q);
endmodule
