// Digital circuit 8Bit Comparator.dig as structural Verilog
module _8Bit_Comparator (
  input  Bit0,
  input  Bit1,
  input  Bit2,
  input  Bit3,
  input  Bit4,
  input  Bit5,
  input  Bit6,
  input  Bit7,
  input  Bit8,
  input  Bit9,
  input  Bit10,
  input  Bit11,
  input  Bit12,
  input  Bit13,
  input  Bit14,
  input  Bit15,
  input  Equal,
  input  Bigger,
  input  Smaller,
  output Out
);

  wire and_1_out, and_2_out, and_3_out, and_4_out, and_5_out, and_6_out, and_7_out, and_8_out, and_9_out,
       and_10_out, and_11_out, and_12_out, and_13_out, and_14_out, and_15_out, and_16_out, and_17_out,
       and_18_out, and_19_out, and_20_out, and_21_out, and_22_out, and_23_out, and_24_out, and_25_out,
       and_26_out, and_27_out, and_28_out, and_29_out, and_30_out, and_31_out, and_32_out, and_33_out,
       and_34_out, and_35_out, and_36_out, and_37_out, and_38_out, and_39_out, and_40_out, or_1_out,
       or_2_out, xnor_1_out, xor_1_out, xor_2_out, xor_3_out, xor_4_out, xor_5_out, xor_6_out, xor_7_out;

  xnor xnor_1 (xnor_1_out, Bit7, Bit15);
  and and_1 (and_1_out, ~Bit7, Bit15);  // And
  and and_2 (and_2_out, Bit7, ~Bit15);  // And
  xor xor_1 (xor_1_out, Bit0, Bit8);
  and and_3 (and_3_out, xor_1_out, Bit8);
  and and_4 (and_4_out, xor_1_out, Bit0);
  xor xor_2 (xor_2_out, Bit1, Bit9);
  and and_5 (and_5_out, xor_2_out, Bit9);
  and and_6 (and_6_out, xor_2_out, Bit1);
  xor xor_3 (xor_3_out, Bit2, Bit10);
  and and_7 (and_7_out, xor_3_out, Bit10);
  and and_8 (and_8_out, xor_3_out, Bit2);
  xor xor_4 (xor_4_out, Bit3, Bit11);
  and and_9 (and_9_out, xor_4_out, Bit11);
  and and_10 (and_10_out, xor_4_out, Bit3);
  xor xor_5 (xor_5_out, Bit4, Bit12);
  and and_11 (and_11_out, xor_5_out, Bit12);
  and and_12 (and_12_out, xor_5_out, Bit4);
  xor xor_6 (xor_6_out, Bit5, Bit13);
  and and_13 (and_13_out, xor_6_out, Bit13);
  and and_14 (and_14_out, xor_6_out, Bit5);
  xor xor_7 (xor_7_out, Bit6, Bit14);
  and and_15 (and_15_out, xor_7_out, Bit14);
  and and_16 (and_16_out, xor_7_out, Bit6);
  and and_17 (and_17_out, ~xor_1_out, and_18_out);  // And
  and and_18 (and_18_out, ~xor_2_out, and_19_out);  // And
  and and_19 (and_19_out, ~xor_3_out, and_20_out);  // And
  and and_20 (and_20_out, ~xor_4_out, and_21_out);  // And
  and and_21 (and_21_out, ~xor_5_out, and_22_out);  // And
  and and_22 (and_22_out, ~xor_6_out, and_23_out);  // And
  and and_23 (and_23_out, ~xor_7_out, xnor_1_out);  // And
  and and_24 (and_24_out, and_3_out, and_18_out);
  and and_25 (and_25_out, and_4_out, and_18_out);
  and and_26 (and_26_out, and_5_out, and_19_out);
  and and_27 (and_27_out, and_6_out, and_19_out);
  and and_28 (and_28_out, and_7_out, and_20_out);
  and and_29 (and_29_out, and_8_out, and_20_out);
  and and_30 (and_30_out, and_9_out, and_21_out);
  and and_31 (and_31_out, and_10_out, and_21_out);
  and and_32 (and_32_out, and_11_out, and_22_out);
  and and_33 (and_33_out, and_12_out, and_22_out);
  and and_34 (and_34_out, and_13_out, and_23_out);
  and and_35 (and_35_out, and_14_out, and_23_out);
  and and_36 (and_36_out, and_15_out, xnor_1_out);
  and and_37 (and_37_out, and_16_out, xnor_1_out);
  or or_1 (or_1_out, and_24_out, and_26_out, and_28_out, and_30_out, and_32_out, and_34_out, and_36_out, and_2_out);
  or or_2 (or_2_out, and_25_out, and_27_out, and_29_out, and_31_out, and_33_out, and_35_out, and_37_out, and_1_out);
  and and_38 (and_38_out, and_17_out, Equal);
  and and_39 (and_39_out, or_1_out, Smaller);
  and and_40 (and_40_out, or_2_out, Bigger);
  or or_3 (Out, and_38_out, and_39_out, and_40_out);
endmodule
