// Digital circuit 8Bit Computer.dig as structural Verilog
module _8Bit_Computer (
  input  clk,
  output out_2,
  output out_3,
  output out_4,
  output out_5,
  output out_6,
  output out_7,
  output out_8,
  output out_9,
  output out_10,
  output out_11,
  output out_12,
  output out_13,
  output out_14,
  output out_15,
  output out_16,
  output out_17,
  output out_18
);

  wire _4bit_computer_command_decoder_1_halt, _4bit_computer_command_decoder_1_jump,
       _4bit_computer_command_decoder_1_jump_if, _4bit_computer_command_decoder_1_load,
       _4bit_computer_command_decoder_1_write, and_1_out, and_2_out, counterpreset_1_ovf, or_1_out, or_2_out,
       or_4_out, t_ff_1_q;
  wire [3:0] Commands_d;
  wire [7:0] _8bit_enable_circuit_1_out, Adresses_d, counterpreset_1_out, Data_d, or_3_out, registerfile_1_db;

  and and_1 (and_1_out, ~or_1_out, clk);  // And
  CounterPreset #(.maxValue(255), .Bits(8)) counterpreset_1 (
    .en(1'b1), .C(and_1_out), .dir(1'b0), .in(Adresses_d), .ld(or_2_out), .clr(1'b0),
    .out(counterpreset_1_out), .ovf(counterpreset_1_ovf));
  or or_1 (or_1_out, counterpreset_1_ovf, _4bit_computer_command_decoder_1_halt);
  ROM #(.AddrBits(8), .Bits(8)) Adresses (.A(counterpreset_1_out), .sel(1'b1), .D(Adresses_d));
  ROM #(.AddrBits(8), .Bits(8)) Data (.A(counterpreset_1_out), .sel(1'b1), .D(Data_d));
  ROM #(.AddrBits(8), .Bits(4)) Commands (.A(counterpreset_1_out), .sel(1'b1), .D(Commands_d));
  _4Bit_Computer_Command_Decoder _4bit_computer_command_decoder_1 (
    .Cmd_Pin0(Commands_d[0]), .Cmd_Pin1(Commands_d[1]), .Cmd_Pin2(Commands_d[2]), .Cmd_Pin3(Commands_d[3]),
    .Write(_4bit_computer_command_decoder_1_write), .Load(_4bit_computer_command_decoder_1_load),
    .Jump(_4bit_computer_command_decoder_1_jump), .Jump_if(_4bit_computer_command_decoder_1_jump_if),
    .Halt(_4bit_computer_command_decoder_1_halt));  // open: Write_num
  or or_2 (or_2_out, and_2_out, _4bit_computer_command_decoder_1_jump);
  assign or_3_out = Data_d | {out_10, out_9, out_8, out_7, out_6, out_5, out_4, out_3} | _8bit_enable_circuit_1_out;  // Or or_3, 8 bits wide
  T_FF t_ff_1 (.T(_4bit_computer_command_decoder_1_load), .C(and_1_out), .Q(t_ff_1_q));  // open: nQ
  or or_4 (or_4_out, or_3_out[0], or_3_out[1], or_3_out[2], or_3_out[3], or_3_out[4], or_3_out[5], or_3_out[6], or_3_out[7]);
  and and_2 (and_2_out, or_4_out, _4bit_computer_command_decoder_1_jump_if);
  _8Bit_enable_circuit _8bit_enable_circuit_1 (
    .In({out_18, out_17, out_16, out_15, out_14, out_13, out_12, out_11}), .En(t_ff_1_q),
    .Out(_8bit_enable_circuit_1_out));
  RegisterFile #(.AddrBits(8), .Bits(8)) registerfile_1 (
    .Din(or_3_out), .we(_4bit_computer_command_decoder_1_write), .Rw(Adresses_d), .C(and_1_out),
    .Ra(Adresses_d), .Rb(or_3_out), .Da({out_18, out_17, out_16, out_15, out_14, out_13, out_12, out_11}),
    .Db(registerfile_1_db));
  // _8Bit_ALU _8bit_alu_1: pin names not known; wires that end beside it: and_1_out, out_3, out_4, out_5, out_6, out_7, out_8, out_9, out_10, out_2

  // Notes on the sheet:
  //   clk: Hz: 50
  //   contents of Adresses (hex, n*v repeats v):
  //   0,1,2,3,4,1,8,2,0,2,1,1,5
  //   contents of Data (hex, n*v repeats v):
  //   a,a,0,1,0,4,0,0,2,0,3
  //   contents of Commands (hex, n*v repeats v):
  //   5*1,8,4,f,5,1,6,1,3
endmodule
