// Digital circuit 8Bit Logic Operations.dig as structural Verilog
module _8Bit_Logic_Operations (
  input  Bit7,
  input  Bit6,
  input  Bit5,
  input  Bit4,
  input  Bit3,
  input  Bit2,
  input  Bit1,
  input  Bit0,
  input  Bit8,
  input  Bit9,
  input  Bit10,
  input  Bit11,
  input  Bit12,
  input  Bit13,
  input  Bit14,
  input  Bit15,
  input  Not,
  input  And,
  input  Or,
  input  Xor,
  output Out
);

  wire and_1_out, and_2_out, and_3_out, and_4_out, and_5_out, and_6_out, and_7_out, and_8_out, or_1_out,
       or_2_out, or_3_out, or_4_out, or_5_out, xor_1_out;

  or or_1 (or_1_out, Bit4, Bit5, Bit6, Bit7);
  or or_2 (or_2_out, Bit8, Bit9, Bit10, Bit11);
  or or_3 (or_3_out, Bit0, Bit1, Bit2, Bit3, or_1_out);
  or or_4 (or_4_out, or_2_out, Bit12, Bit13, Bit14, Bit15);
  and and_1 (and_1_out, ~or_3_out, Not);  // And
  and and_2 (and_2_out, or_3_out, And);
  and and_3 (and_3_out, or_3_out, Or);
  and and_4 (and_4_out, or_3_out, Xor);
  and and_5 (and_5_out, or_4_out, And);
  and and_6 (and_6_out, or_4_out, Or);
  and and_7 (and_7_out, or_4_out, Xor);
  and and_8 (and_8_out, and_2_out, and_5_out);
  or or_5 (or_5_out, and_3_out, and_6_out);
  xor xor_1 (xor_1_out, and_4_out, and_7_out);
  or or_6 (Out, and_1_out, and_8_out, or_5_out, xor_1_out);
endmodule
