// Digital circuit 8Bit Logic Operations.dig as structural Verilog
module _8Bit_Logic_Operations (
  input  [7:0] A,
  input  [7:0] B,
  input  [1:0] CMD,
  output [7:0] Q
);

  wire _7404_1_pin2, _7404_1_pin4, _7404_1_pin6, _7404_1_pin8, _7404_1_pin10, _7404_1_pin12, _7404_2_pin2,
       _7404_2_pin4, _7408_1_pin3, _7408_1_pin6, _7408_1_pin8, _7408_1_pin11, _7408_2_pin3, _7408_2_pin6,
       _7408_2_pin8, _7408_2_pin11, _7432_1_pin3, _7432_1_pin6, _7432_1_pin8, _7432_1_pin11, _7432_2_pin3,
       _7432_2_pin6, _7432_2_pin8, _7432_2_pin11, _7486_1_pin3, _7486_1_pin6, _7486_1_pin8, _7486_1_pin11,
       _7486_2_pin3, _7486_2_pin6, _7486_2_pin8, _7486_2_pin11;

  _7408 _7408_1 (
    .pin1(A[0]), .pin2(B[0]), .pin3(_7408_1_pin3), .pin4(A[1]), .pin5(B[1]), .pin6(_7408_1_pin6),
    .pin7(1'b0), .pin8(_7408_1_pin8), .pin9(A[2]), .pin10(B[2]), .pin11(_7408_1_pin11), .pin12(A[3]),
    .pin13(B[3]), .pin14(1'b1));
  _7486 _7486_1 (
    .pin1(A[0]), .pin2(B[0]), .pin3(_7486_1_pin3), .pin4(A[1]), .pin5(B[1]), .pin6(_7486_1_pin6),
    .pin7(1'b0), .pin8(_7486_1_pin8), .pin9(A[2]), .pin10(B[2]), .pin11(_7486_1_pin11), .pin12(A[3]),
    .pin13(B[3]), .pin14(1'b1));
  _7432 _7432_1 (
    .pin1(A[0]), .pin2(B[0]), .pin3(_7432_1_pin3), .pin4(A[1]), .pin5(B[1]), .pin6(_7432_1_pin6),
    .pin7(1'b0), .pin8(_7432_1_pin8), .pin9(A[2]), .pin10(B[2]), .pin11(_7432_1_pin11), .pin12(A[3]),
    .pin13(B[3]), .pin14(1'b1));
  _7404 _7404_1 (
    .pin1(A[0]), .pin2(_7404_1_pin2), .pin3(A[1]), .pin4(_7404_1_pin4), .pin5(A[2]), .pin6(_7404_1_pin6),
    .pin7(1'b0), .pin8(_7404_1_pin8), .pin9(A[3]), .pin10(_7404_1_pin10), .pin11(A[4]),
    .pin12(_7404_1_pin12), .pin13(A[5]), .pin14(1'b1));
  _7408 _7408_2 (
    .pin1(A[4]), .pin2(B[4]), .pin3(_7408_2_pin3), .pin4(A[5]), .pin5(B[5]), .pin6(_7408_2_pin6),
    .pin7(1'b0), .pin8(_7408_2_pin8), .pin9(A[6]), .pin10(B[6]), .pin11(_7408_2_pin11), .pin12(A[7]),
    .pin13(B[7]), .pin14(1'b1));
  _7486 _7486_2 (
    .pin1(A[4]), .pin2(B[4]), .pin3(_7486_2_pin3), .pin4(A[5]), .pin5(B[5]), .pin6(_7486_2_pin6),
    .pin7(1'b0), .pin8(_7486_2_pin8), .pin9(A[6]), .pin10(B[6]), .pin11(_7486_2_pin11), .pin12(A[7]),
    .pin13(B[7]), .pin14(1'b1));
  _7432 _7432_2 (
    .pin1(A[4]), .pin2(B[4]), .pin3(_7432_2_pin3), .pin4(A[5]), .pin5(B[5]), .pin6(_7432_2_pin6),
    .pin7(1'b0), .pin8(_7432_2_pin8), .pin9(A[6]), .pin10(B[6]), .pin11(_7432_2_pin11), .pin12(A[7]),
    .pin13(B[7]), .pin14(1'b1));
  _7404 _7404_2 (
    .pin1(A[6]), .pin2(_7404_2_pin2), .pin3(A[7]), .pin4(_7404_2_pin4), .pin5(1'b0), .pin7(1'b0),
    .pin9(1'b0), .pin11(1'b0), .pin13(1'b0), .pin14(1'b1));  // open: pin6, pin8, pin10, pin12
  _74153 _74153_1 (
    .pin1(1'b0), .pin2(CMD[1]), .pin3(_7408_2_pin11), .pin4(_7486_2_pin11), .pin5(_7432_2_pin11),
    .pin6(_7404_2_pin4), .pin7(Q[7]), .pin8(1'b0), .pin9(Q[6]), .pin10(_7404_2_pin2), .pin11(_7432_2_pin8),
    .pin12(_7486_2_pin8), .pin13(_7408_2_pin8), .pin14(CMD[0]), .pin15(1'b0), .pin16(1'b1));
  _74153 _74153_2 (
    .pin1(1'b0), .pin2(CMD[1]), .pin3(_7408_2_pin6), .pin4(_7486_2_pin6), .pin5(_7432_2_pin6),
    .pin6(_7404_1_pin8), .pin7(Q[5]), .pin8(1'b0), .pin9(Q[4]), .pin10(_7404_1_pin10), .pin11(_7432_2_pin3),
    .pin12(_7486_2_pin3), .pin13(_7408_2_pin3), .pin14(CMD[0]), .pin15(1'b0), .pin16(1'b1));
  _74153 _74153_3 (
    .pin1(1'b0), .pin2(CMD[1]), .pin3(_7408_1_pin11), .pin4(_7486_1_pin11), .pin5(_7432_1_pin11),
    .pin6(_7404_1_pin12), .pin7(Q[3]), .pin8(1'b0), .pin9(Q[2]), .pin10(_7404_1_pin6), .pin11(_7432_1_pin8),
    .pin12(_7486_1_pin8), .pin13(_7408_1_pin8), .pin14(CMD[0]), .pin15(1'b0), .pin16(1'b1));
  _74153 _74153_4 (
    .pin1(1'b0), .pin2(CMD[1]), .pin3(_7408_1_pin6), .pin4(_7486_1_pin6), .pin5(_7432_1_pin6),
    .pin6(_7404_1_pin4), .pin7(Q[1]), .pin8(1'b0), .pin9(Q[0]), .pin10(_7404_1_pin2), .pin11(_7432_1_pin3),
    .pin12(_7486_1_pin3), .pin13(_7408_1_pin3), .pin14(CMD[0]), .pin15(1'b0), .pin16(1'b1));
  // _74541 _74541_1: pin names not known
  // _74688 _74688_1: pin names not known

  // Notes on the sheet:
  //   00 -> !A
  //   01 -> A+B
  //   10 -> |A-B|
  //   11 -> A*B
  //   'S' series
endmodule
