// Digital circuit 8 By 8 Pixel Display.dig as structural Verilog
module _8_By_8_Pixel_Display (
  input  [7:0] DAT,
  input  [15:0] ADR,
  input  STR,
  input  LD,
  input  CLK,
  output [63:0] OUT,
  output [7:0] Q
);

  wire and_1_out, and_2_out, and_3_out, and_4_out, and_5_out, and_6_out, and_7_out, and_8_out, and_9_out,
       and_10_out, and_11_out, and_12_out, and_13_out, and_14_out, and_15_out, and_16_out, comparator_1_eq,
       comparator_2_eq, comparator_3_eq, comparator_4_eq, comparator_5_eq, comparator_6_eq, comparator_7_eq,
       comparator_8_eq, d_ff_1_q, delay_1_out, not_1_out;
  wire [7:0] driver_1_out, register_9_q;

  not not_1 (not_1_out, CLK);
  D_FF d_ff_1 (.D(LD), .C(not_1_out), .Q(d_ff_1_q));  // open: nQ
  Comparator #(.Bits(8)) comparator_1 (.a(ADR[7:0]), .b({8{1'b0}}), .eq(comparator_1_eq));  // open: gt, lt
  Comparator #(.Bits(8)) comparator_2 (.a(ADR[7:0]), .b(8'h1), .eq(comparator_2_eq));  // open: gt, lt
  Comparator #(.Bits(8)) comparator_3 (.a(ADR[7:0]), .b(8'h2), .eq(comparator_3_eq));  // open: gt, lt
  Comparator #(.Bits(8)) comparator_4 (.a(ADR[7:0]), .b(8'h3), .eq(comparator_4_eq));  // open: gt, lt
  and and_1 (and_1_out, STR, comparator_1_eq);
  and and_2 (and_2_out, STR, comparator_2_eq);
  and and_3 (and_3_out, STR, comparator_3_eq);
  and and_4 (and_4_out, STR, comparator_4_eq);
  Register #(.Bits(8)) register_1 (.D(DAT), .C(and_1_out), .en(1'b1), .Q(OUT[7:0]));
  and and_5 (and_5_out, comparator_1_eq, d_ff_1_q);
  Register #(.Bits(8)) register_2 (.D(DAT), .C(and_2_out), .en(1'b1), .Q(OUT[15:8]));
  and and_6 (and_6_out, comparator_2_eq, d_ff_1_q);
  Register #(.Bits(8)) register_3 (.D(DAT), .C(and_3_out), .en(1'b1), .Q(OUT[23:16]));
  and and_7 (and_7_out, comparator_3_eq, d_ff_1_q);
  Register #(.Bits(8)) register_4 (.D(DAT), .C(and_4_out), .en(1'b1), .Q(OUT[31:24]));
  and and_8 (and_8_out, comparator_4_eq, d_ff_1_q);
  assign driver_1_out = and_5_out ? OUT[7:0] : 8'bz;  // Driver driver_1
  assign driver_1_out = and_6_out ? OUT[15:8] : 8'bz;  // Driver driver_2
  assign driver_1_out = and_7_out ? OUT[23:16] : 8'bz;  // Driver driver_3
  assign driver_1_out = and_8_out ? OUT[31:24] : 8'bz;  // Driver driver_4
  Comparator #(.Bits(8)) comparator_5 (.a(ADR[7:0]), .b(8'h4), .eq(comparator_5_eq));  // open: gt, lt
  Comparator #(.Bits(8)) comparator_6 (.a(ADR[7:0]), .b(8'h5), .eq(comparator_6_eq));  // open: gt, lt
  Comparator #(.Bits(8)) comparator_7 (.a(ADR[7:0]), .b(8'h6), .eq(comparator_7_eq));  // open: gt, lt
  Comparator #(.Bits(8)) comparator_8 (.a(ADR[7:0]), .b(8'h7), .eq(comparator_8_eq));  // open: gt, lt
  and and_9 (and_9_out, STR, comparator_5_eq);
  and and_10 (and_10_out, STR, comparator_6_eq);
  and and_11 (and_11_out, STR, comparator_7_eq);
  and and_12 (and_12_out, STR, comparator_8_eq);
  Register #(.Bits(8)) register_5 (.D(DAT), .C(and_9_out), .en(1'b1), .Q(OUT[39:32]));
  and and_13 (and_13_out, comparator_5_eq, d_ff_1_q);
  Register #(.Bits(8)) register_6 (.D(DAT), .C(and_10_out), .en(1'b1), .Q(OUT[47:40]));
  and and_14 (and_14_out, comparator_6_eq, d_ff_1_q);
  Register #(.Bits(8)) register_7 (.D(DAT), .C(and_11_out), .en(1'b1), .Q(OUT[55:48]));
  and and_15 (and_15_out, comparator_7_eq, d_ff_1_q);
  Register #(.Bits(8)) register_8 (.D(DAT), .C(and_12_out), .en(1'b1), .Q(OUT[63:56]));
  and and_16 (and_16_out, comparator_8_eq, d_ff_1_q);
  Delay #(.delayTime(2)) delay_1 (.in(d_ff_1_q), .out(delay_1_out));
  assign driver_1_out = and_13_out ? OUT[39:32] : 8'bz;  // Driver driver_5
  assign driver_1_out = and_14_out ? OUT[47:40] : 8'bz;  // Driver driver_6
  assign driver_1_out = and_15_out ? OUT[55:48] : 8'bz;  // Driver driver_7
  assign driver_1_out = and_16_out ? OUT[63:56] : 8'bz;  // Driver driver_8
  Register #(.Bits(8)) register_9 (.D(driver_1_out), .C(delay_1_out), .en(1'b1), .Q(register_9_q));
  assign Q = d_ff_1_q ? register_9_q : 8'bz;  // Driver driver_9

  // Notes on the sheet:
  //   this splitter just discards
  //   the last 8 bits of the address bus
  //   DAT
  //   ADR
  //   LD
  //   STR
endmodule
