// Digital circuit 8 to 16 bit bus width converter.dig as structural Verilog
module _8_to_16_bit_bus_width_converter (
  input  [7:0] In,
  input  Str_1,
  input  Str_2,
  output [15:0] Q
);

  Register #(.Bits(8)) register_1 (.D(In), .C(Str_1), .en(1'b1), .Q(Q[7:0]));
  Register #(.Bits(8)) register_2 (.D(In), .C(Str_2), .en(1'b1), .Q(Q[15:8]));
endmodule
