// Digital circuit Adder Subtractor.dig as structural Verilog
module Adder_Subtractor (
  input  C_in,
  input  [7:0] A,
  input  [7:0] B,
  input  ADD,
  input  ADC,
  input  SUB,
  input  CLK,
  output [7:0] Q,
  output C_8,
  output F,
  output STC,
  output STF
);

  wire add_1_c_o, add_2_c_o, add_3_c_o, and_1_out, d_ff_1_q, d_ff_2_q, d_ff_3_q, d_ff_4_nq, d_ff_4_q,
       not_1_out, or_1_out, or_2_out, xor_2_out;
  wire [2:0] add_2_s;
  wire [3:0] add_1_s;
  wire [7:0] register_1_q, xor_1_out;
  wire [7:7] add_3_s;

  or or_1 (or_1_out, ADD, ADC, SUB);
  and and_1 (and_1_out, C_in, ADC);
  not not_1 (not_1_out, CLK);
  D_FF d_ff_1 (.D(or_1_out), .C(not_1_out), .Q(d_ff_1_q));  // open: nQ
  or or_2 (or_2_out, and_1_out, SUB);
  assign xor_1_out = B ^ {8{SUB}};  // XOr xor_1, 8 bits wide
  Add #(.Bits(4)) add_1 (.a(A[3:0]), .b(xor_1_out[3:0]), .c_i(or_2_out), .s(add_1_s), .c_o(add_1_c_o));
  Add #(.Bits(3)) add_2 (.a(A[6:4]), .b(xor_1_out[6:4]), .c_i(add_1_c_o), .s(add_2_s), .c_o(add_2_c_o));
  Add add_3 (.a(A[7]), .b(xor_1_out[7]), .c_i(add_2_c_o), .s(add_3_s[7]), .c_o(add_3_c_o));
  xor xor_2 (xor_2_out, add_3_c_o, add_2_c_o);
  Register #(.Bits(8)) register_1 (.D({add_3_s[7], add_2_s, add_1_s}), .C(d_ff_1_q), .en(1'b1), .Q(register_1_q));
  D_FF d_ff_2 (.D(add_3_c_o), .C(d_ff_1_q), .Q(d_ff_2_q));  // open: nQ
  D_FF d_ff_3 (.D(xor_2_out), .C(d_ff_1_q), .Q(d_ff_3_q));  // open: nQ
  D_FF d_ff_4 (.D(SUB), .C(d_ff_1_q), .Q(d_ff_4_q), .nQ(d_ff_4_nq));
  assign Q = d_ff_1_q ? register_1_q : 8'bz;  // Driver driver_1
  assign C_8 = d_ff_1_q ? d_ff_2_q : 1'bz;  // Driver driver_2
  assign F = d_ff_1_q ? d_ff_3_q : 1'bz;  // Driver driver_3
  assign STC = d_ff_1_q ? d_ff_4_nq : 1'bz;  // Driver driver_4
  assign STF = d_ff_1_q ? d_ff_4_q : 1'bz;  // Driver driver_5

  // Notes on the sheet:
  //   Add with carry <-
  //   An XOR gate inverts one input if the other one
  //   is high. This is needed for 2's complement subtraction.
  //   Makes sure that 
  //   every XOR gate 
  //   has SUB as an 
  //   input, since it is 
  //   8bit wide it will only 
  //   accept 8bit inputs.
  //   The split adder + the xor gate are for 
  //   Overflow detection during a subtraction
  //   -> the normal 8bit output
  //   -> the carry output incase the adder 
  //   output exceeds the 8 bit limit
  //   -> overflow of the subtractor
endmodule
