// Digital circuit Barrel Shift Register.dig as structural Verilog
module Barrel_Shift_Register (
  input  [7:0] A,
  input  [7:0] DIS,
  input  SFT,
  input  SFC,
  input  CLK,
  output [7:0] Q
);

  wire and_1_out, and_2_out, and_3_out, and_4_out, and_5_out, and_6_out, and_7_out, d_ff_1_q,
       multiplexer_1_out, multiplexer_2_out, multiplexer_3_out, multiplexer_4_out, multiplexer_5_out,
       multiplexer_6_out, multiplexer_7_out, multiplexer_8_out, multiplexer_9_out, multiplexer_10_out,
       multiplexer_11_out, multiplexer_12_out, multiplexer_13_out, multiplexer_14_out, multiplexer_15_out,
       multiplexer_16_out, not_1_out, or_1_out;
  wire [7:0] multiplexer_17_out, register_1_q;

  or or_1 (or_1_out, SFT, SFC);
  not not_1 (not_1_out, CLK);
  D_FF d_ff_1 (.D(or_1_out), .C(not_1_out), .Q(d_ff_1_q));  // open: nQ
  and and_1 (and_1_out, A[7], SFC);
  Multiplexer multiplexer_1 (.sel(DIS[0]), .in_0(A[7]), .in_1(A[6]), .out(multiplexer_1_out));
  Multiplexer multiplexer_2 (.sel(DIS[0]), .in_0(A[6]), .in_1(A[5]), .out(multiplexer_2_out));
  Multiplexer multiplexer_3 (.sel(DIS[0]), .in_0(A[5]), .in_1(A[4]), .out(multiplexer_3_out));
  Multiplexer multiplexer_4 (.sel(DIS[0]), .in_0(A[4]), .in_1(A[3]), .out(multiplexer_4_out));
  Multiplexer multiplexer_5 (.sel(DIS[0]), .in_0(A[3]), .in_1(A[2]), .out(multiplexer_5_out));
  Multiplexer multiplexer_6 (.sel(DIS[0]), .in_0(A[2]), .in_1(A[1]), .out(multiplexer_6_out));
  Multiplexer multiplexer_7 (.sel(DIS[0]), .in_0(A[1]), .in_1(A[0]), .out(multiplexer_7_out));
  Multiplexer multiplexer_8 (.sel(DIS[0]), .in_0(A[0]), .in_1(and_1_out), .out(multiplexer_8_out));
  and and_2 (and_2_out, multiplexer_1_out, SFC);
  and and_3 (and_3_out, multiplexer_2_out, SFC);
  Multiplexer multiplexer_9 (.sel(DIS[1]), .in_0(multiplexer_1_out), .in_1(multiplexer_3_out), .out(multiplexer_9_out));
  Multiplexer multiplexer_10 (
    .sel(DIS[1]), .in_0(multiplexer_2_out), .in_1(multiplexer_4_out), .out(multiplexer_10_out));
  Multiplexer multiplexer_11 (
    .sel(DIS[1]), .in_0(multiplexer_3_out), .in_1(multiplexer_5_out), .out(multiplexer_11_out));
  Multiplexer multiplexer_12 (
    .sel(DIS[1]), .in_0(multiplexer_4_out), .in_1(multiplexer_6_out), .out(multiplexer_12_out));
  Multiplexer multiplexer_13 (
    .sel(DIS[1]), .in_0(multiplexer_5_out), .in_1(multiplexer_7_out), .out(multiplexer_13_out));
  Multiplexer multiplexer_14 (
    .sel(DIS[1]), .in_0(multiplexer_6_out), .in_1(multiplexer_8_out), .out(multiplexer_14_out));
  Multiplexer multiplexer_15 (.sel(DIS[1]), .in_0(multiplexer_7_out), .in_1(and_2_out), .out(multiplexer_15_out));
  Multiplexer multiplexer_16 (.sel(DIS[1]), .in_0(multiplexer_8_out), .in_1(and_3_out), .out(multiplexer_16_out));
  and and_4 (and_4_out, multiplexer_9_out, SFC);
  and and_5 (and_5_out, multiplexer_10_out, SFC);
  and and_6 (and_6_out, multiplexer_11_out, SFC);
  and and_7 (and_7_out, multiplexer_12_out, SFC);
  Multiplexer multiplexer_17 (
    .sel(DIS[2]), .in_0(multiplexer_9_out), .in_1(multiplexer_13_out), .out(multiplexer_17_out[7]));
  Multiplexer multiplexer_18 (
    .sel(DIS[2]), .in_0(multiplexer_10_out), .in_1(multiplexer_14_out), .out(multiplexer_17_out[6]));
  Multiplexer multiplexer_19 (
    .sel(DIS[2]), .in_0(multiplexer_11_out), .in_1(multiplexer_15_out), .out(multiplexer_17_out[5]));
  Multiplexer multiplexer_20 (
    .sel(DIS[2]), .in_0(multiplexer_12_out), .in_1(multiplexer_16_out), .out(multiplexer_17_out[4]));
  Multiplexer multiplexer_21 (.sel(DIS[2]), .in_0(multiplexer_13_out), .in_1(and_4_out), .out(multiplexer_17_out[3]));
  Multiplexer multiplexer_22 (.sel(DIS[2]), .in_0(multiplexer_14_out), .in_1(and_5_out), .out(multiplexer_17_out[2]));
  Multiplexer multiplexer_23 (.sel(DIS[2]), .in_0(multiplexer_15_out), .in_1(and_6_out), .out(multiplexer_17_out[1]));
  Multiplexer multiplexer_24 (.sel(DIS[2]), .in_0(multiplexer_16_out), .in_1(and_7_out), .out(multiplexer_17_out[0]));
  Register #(.Bits(8)) register_1 (.D(multiplexer_17_out), .C(d_ff_1_q), .en(1'b1), .Q(register_1_q));
  assign Q = d_ff_1_q ? register_1_q : 8'bz;  // Driver driver_1

  // Notes on the sheet:
  //   DIS: The distance that A should be shifted,
  //   this value will come from the data bus
  //   SFT: The normal shit command
  //   SFC: Shift Circular
endmodule
