// Digital circuit Binary AND.dig as structural Verilog
module Binary_AND (
  input  [7:0] A,
  input  [7:0] B,
  input  CLK,
  input  EN,
  output [7:0] Q
);

  wire d_ff_1_q, d_ff_2_q, or_1_out, or_2_out;
  wire [0:0] and_1_out;

  or or_1 (or_1_out, A[0], A[1], A[2], A[3], A[4], A[5], A[6], A[7]);
  or or_2 (or_2_out, B[0], B[1], B[2], B[3], B[4], B[5], B[6], B[7]);
  and and_1 (and_1_out[0], or_1_out, or_2_out);
  D_FF d_ff_1 (.D(EN), .C(CLK), .Q(d_ff_1_q));  // open: nQ
  D_FF d_ff_2 (.D(d_ff_1_q), .C(CLK), .Q(d_ff_2_q));  // open: nQ
  assign Q = d_ff_2_q ? {{7{1'b0}}, and_1_out[0]} : 8'bz;  // Driver driver_1
endmodule
