// Digital circuit Binary NOT.dig as structural Verilog
module Binary_NOT (
  input  [7:0] A,
  input  EN,
  input  CLK,
  output [7:0] Q
);

  wire d_ff_1_q, not_1_out, not_2_out, or_1_out;
  wire [0:0] d_ff_2_q;

  not not_1 (not_1_out, CLK);
  or or_1 (or_1_out, A[0], A[1], A[2], A[3], A[4], A[5], A[6], A[7]);
  D_FF d_ff_1 (.D(EN), .C(not_1_out), .Q(d_ff_1_q));  // open: nQ
  not not_2 (not_2_out, or_1_out);
  D_FF d_ff_2 (.D(not_2_out), .C(d_ff_1_q), .Q(d_ff_2_q[0]));  // open: nQ
  assign Q = d_ff_1_q ? {{7{1'b0}}, d_ff_2_q[0]} : 8'bz;  // Driver driver_1
endmodule
