// Digital circuit Bitwise AND.dig as structural Verilog
module Bitwise_AND (
  input  [7:0] A,
  input  [7:0] B,
  input  EN,
  input  CLK,
  output [7:0] Q
);

  wire d_ff_1_q, not_1_out;
  wire [7:0] and_1_out, register_1_q;

  assign and_1_out = A & B;  // And and_1, 8 bits wide
  not not_1 (not_1_out, CLK);
  D_FF d_ff_1 (.D(EN), .C(not_1_out), .Q(d_ff_1_q));  // open: nQ
  Register #(.Bits(8)) register_1 (.D(and_1_out), .C(d_ff_1_q), .en(1'b1), .Q(register_1_q));
  assign Q = d_ff_1_q ? register_1_q : 8'bz;  // Driver driver_1
endmodule
