// Digital circuit Bus Interface.dig as structural Verilog
module Bus_Interface (
  input  [7:0] IN,
  input  EN,
  output [7:0] Q
);

  assign Q = IN & {8{EN}};  // And and_1, 8 bits wide

  // Notes on the sheet:
  //   For making an 
  //   8bit signal
  //   out of 1bit
endmodule
