// Digital circuit CPU.dig as structural Verilog
module CPU (
  input  clk,
  input  clk_2
);

  wire alu_1_p5, button_7_out, button_8_out, button_9_out, comparator_1_eq, comparator_2_eq, comparator_3_eq,
       comparator_4_eq, comparator_5_eq, comparator_6_eq, comparator_7_eq, comparator_8_eq, comparator_9_eq,
       comparator_10_eq, comparator_11_eq, comparator_12_eq, comparator_13_eq, comparator_14_eq,
       comparator_15_eq, diodeforward_1_out, multiplexer_1_out, or_1_out, or_2_out;
  wire [1:0] dipswitch_4_out;
  wire [3:0] alu_1_p6, alu_1_p6_2, flash_memory_1_q_adr, flash_memory_1_q_adr_2, flash_memory_1_q_adr_3,
       flash_memory_1_q_adr_4, flash_memory_1_q_cmd, flash_memory_1_q_cmd_2, flash_memory_1_q_dat,
       flash_memory_1_q_dat_2, programme_counter_1_ln_2, programme_counter_1_ln_3;
  wire [5:0] button_2_out;
  wire [7:0] alu_1_p7, dipswitch_3_out, programme_counter_1_ln, register_1_val, register_2_val;
  wire [63:0] _8_by_8_pixel_display_1_out;

  Button button_1 (.out(button_2_out[1]));
  Button button_2 (.out(button_2_out[2]));
  Button button_3 (.out(button_2_out[4]));
  Button button_4 (.out(button_2_out[5]));
  Button button_5 (.out(button_2_out[0]));
  Button button_6 (.out(button_2_out[3]));
  Button button_7 (.out(button_7_out));
  Multiplexer #(.Selector_Bits(2)) multiplexer_1 (
    .sel(dipswitch_4_out), .in_0(1'b0), .in_1(button_7_out), .in_2(clk), .in_3(clk_2), .out(multiplexer_1_out));
  or or_1 (or_1_out, multiplexer_1_out, button_9_out);
  Seven_Seg_Hex seven_seg_hex_1 (.d(alu_1_p6_2), .dp(1'b0));
  LED led_1 (.in(alu_1_p6_2[1]));
  LED led_2 (.in(alu_1_p6_2[2]));
  LED led_3 (.in(alu_1_p6_2[3]));
  Seven_Seg_Hex seven_seg_hex_2 (.d(alu_1_p7[7:4]), .dp(1'b0));
  LED led_4 (.in(alu_1_p7[5]));
  LED led_5 (.in(alu_1_p7[6]));
  LED led_6 (.in(alu_1_p7[7]));
  Seven_Seg_Hex seven_seg_hex_3 (.d(register_1_val[7:4]), .dp(1'b0));
  LED led_7 (.in(register_1_val[5]));
  LED led_8 (.in(register_1_val[6]));
  LED led_9 (.in(register_1_val[7]));
  DipSwitch dipswitch_1 (.out(dipswitch_3_out[5]));
  DipSwitch dipswitch_2 (.out(dipswitch_3_out[6]));
  DipSwitch dipswitch_3 (.out(dipswitch_3_out[7]));
  DipSwitch dipswitch_4 (.out(dipswitch_4_out[1]));
  DipSwitch #(.dipDefault("true")) dipswitch_5 (.out(dipswitch_4_out[0]));
  Seven_Seg_Hex seven_seg_hex_4 (.d(alu_1_p6), .dp(1'b0));
  LED led_10 (.in(alu_1_p6_2[0]));
  LED led_11 (.in(alu_1_p6[2]));
  LED led_12 (.in(alu_1_p6[3]));
  Seven_Seg_Hex seven_seg_hex_5 (.d(alu_1_p7[3:0]), .dp(1'b0));
  LED led_13 (.in(alu_1_p7[4]));
  LED led_14 (.in(alu_1_p7[2]));
  LED led_15 (.in(alu_1_p7[3]));
  Seven_Seg_Hex seven_seg_hex_6 (.d(register_1_val[3:0]), .dp(1'b0));
  LED led_16 (.in(register_1_val[4]));
  LED led_17 (.in(register_1_val[2]));
  LED led_18 (.in(register_1_val[3]));
  DipSwitch dipswitch_6 (.out(dipswitch_3_out[2]));
  DipSwitch dipswitch_7 (.out(dipswitch_3_out[3]));
  DipSwitch dipswitch_8 (.out(dipswitch_3_out[4]));
  LED led_19 (.in(alu_1_p6[1]));
  LED led_20 (.in(alu_1_p6[0]));
  LED led_21 (.in(alu_1_p7[1]));
  LED led_22 (.in(alu_1_p7[0]));
  LED led_23 (.in(register_1_val[1]));
  LED led_24 (.in(register_1_val[0]));
  DipSwitch dipswitch_9 (.out(dipswitch_3_out[0]));
  DipSwitch dipswitch_10 (.out(dipswitch_3_out[1]));
  Seven_Seg_Hex seven_seg_hex_7 (.d(flash_memory_1_q_cmd_2), .dp(1'b0));
  Button button_8 (.out(button_8_out));
  LED led_25 (.in(flash_memory_1_q_cmd_2[3]));
  Seven_Seg_Hex seven_seg_hex_8 (.d(flash_memory_1_q_cmd), .dp(1'b0));
  LED led_26 (.in(flash_memory_1_q_cmd_2[1]));
  LED led_27 (.in(flash_memory_1_q_cmd_2[0]));
  LED led_28 (.in(flash_memory_1_q_cmd_2[2]));
  LED led_29 (.in(flash_memory_1_q_cmd[1]));
  LED led_30 (.in(flash_memory_1_q_cmd[0]));
  LED led_31 (.in(flash_memory_1_q_cmd[2]));
  LED led_32 (.in(flash_memory_1_q_cmd[3]));
  Comparator #(.Bits(8)) comparator_1 (
    .a({flash_memory_1_q_cmd_2, flash_memory_1_q_cmd}), .b(8'h1), .eq(comparator_1_eq));  // open: gt, lt
  Comparator #(.Bits(8)) comparator_2 (
    .a({flash_memory_1_q_cmd_2, flash_memory_1_q_cmd}), .b(8'h2), .eq(comparator_2_eq));  // open: gt, lt
  Comparator #(.Bits(8)) comparator_3 (
    .a({flash_memory_1_q_cmd_2, flash_memory_1_q_cmd}), .b(8'h3), .eq(comparator_3_eq));  // open: gt, lt
  Comparator #(.Bits(8)) comparator_4 (
    .a({flash_memory_1_q_cmd_2, flash_memory_1_q_cmd}), .b(8'h4), .eq(comparator_4_eq));  // open: gt, lt
  Comparator #(.Bits(8)) comparator_5 (
    .a({flash_memory_1_q_cmd_2, flash_memory_1_q_cmd}), .b(8'h5), .eq(comparator_5_eq));  // open: gt, lt
  Comparator #(.Bits(8)) comparator_6 (
    .a({flash_memory_1_q_cmd_2, flash_memory_1_q_cmd}), .b(8'h6), .eq(comparator_6_eq));  // open: gt, lt
  Comparator #(.Bits(8)) comparator_7 (
    .a({flash_memory_1_q_cmd_2, flash_memory_1_q_cmd}), .b(8'h7), .eq(comparator_7_eq));  // open: gt, lt
  Comparator #(.Bits(8)) comparator_8 (
    .a({flash_memory_1_q_cmd_2, flash_memory_1_q_cmd}), .b(8'h26), .eq(comparator_8_eq));  // open: gt, lt
  Comparator #(.Bits(8)) comparator_9 (
    .a({flash_memory_1_q_cmd_2, flash_memory_1_q_cmd}), .b(8'h27), .eq(comparator_9_eq));  // open: gt, lt
  Comparator #(.Bits(8)) comparator_10 (
    .a({flash_memory_1_q_cmd_2, flash_memory_1_q_cmd}), .b(8'h28), .eq(comparator_10_eq));  // open: gt, lt
  Comparator #(.Bits(8)) comparator_11 (
    .a({flash_memory_1_q_cmd_2, flash_memory_1_q_cmd}), .b(8'h29), .eq(comparator_11_eq));  // open: gt, lt
  Comparator #(.Bits(8)) comparator_12 (
    .a({flash_memory_1_q_cmd_2, flash_memory_1_q_cmd}), .b(8'h2a), .eq(comparator_12_eq));  // open: gt, lt
  Comparator #(.Bits(8)) comparator_13 (
    .a({flash_memory_1_q_cmd_2, flash_memory_1_q_cmd}), .b(8'h2b), .eq(comparator_13_eq));  // open: gt, lt
  Comparator #(.Bits(8)) comparator_14 (
    .a({flash_memory_1_q_cmd_2, flash_memory_1_q_cmd}), .b(8'h2c), .eq(comparator_14_eq));  // open: gt, lt
  Comparator #(.Bits(8)) comparator_15 (
    .a({flash_memory_1_q_cmd_2, flash_memory_1_q_cmd}), .b(8'h2d), .eq(comparator_15_eq));  // open: gt, lt
  Seven_Seg_Hex seven_seg_hex_9 (.d(programme_counter_1_ln_3), .dp(1'b0));
  LED led_33 (.in(programme_counter_1_ln_3[2]));
  LED led_34 (.in(programme_counter_1_ln_3[3]));
  LED led_35 (.in(programme_counter_1_ln_3[1]));
  Seven_Seg_Hex seven_seg_hex_10 (.d(flash_memory_1_q_dat_2), .dp(1'b0));
  LED led_36 (.in(flash_memory_1_q_dat_2[1]));
  LED led_37 (.in(flash_memory_1_q_dat_2[2]));
  LED led_38 (.in(flash_memory_1_q_dat_2[3]));
  or or_2 (or_2_out, button_8_out, comparator_8_eq);
  Seven_Seg_Hex seven_seg_hex_11 (.d(programme_counter_1_ln_2), .dp(1'b0));
  LED led_39 (.in(programme_counter_1_ln_3[0]));
  LED led_40 (.in(programme_counter_1_ln_2[2]));
  LED led_41 (.in(programme_counter_1_ln_2[3]));
  Seven_Seg_Hex seven_seg_hex_12 (.d(flash_memory_1_q_dat), .dp(1'b0));
  LED led_42 (.in(flash_memory_1_q_dat_2[0]));
  LED led_43 (.in(flash_memory_1_q_dat[2]));
  LED led_44 (.in(flash_memory_1_q_dat[3]));
  Seven_Seg_Hex seven_seg_hex_13 (.d(programme_counter_1_ln[7:4]), .dp(1'b0));
  LED led_45 (.in(programme_counter_1_ln_2[1]));
  LED led_46 (.in(programme_counter_1_ln_2[0]));
  LED led_47 (.in(programme_counter_1_ln[7]));
  LED led_48 (.in(flash_memory_1_q_dat[1]));
  LED led_49 (.in(flash_memory_1_q_dat[0]));
  LED led_50 (.in(flash_memory_1_q_adr_4[3]));
  DiodeForward diodeforward_1 (.in(comparator_7_eq), .out(diodeforward_1_out));
  DiodeForward diodeforward_2 (.in(comparator_9_eq), .out(diodeforward_1_out));
  DiodeForward diodeforward_3 (.in(comparator_10_eq), .out(diodeforward_1_out));
  DiodeForward diodeforward_4 (.in(comparator_12_eq), .out(diodeforward_1_out));
  DiodeForward diodeforward_5 (.in(comparator_14_eq), .out(diodeforward_1_out));
  DiodeForward diodeforward_6 (.in(comparator_15_eq), .out(diodeforward_1_out));
  Seven_Seg_Hex seven_seg_hex_14 (.d(programme_counter_1_ln[3:0]), .dp(1'b0));
  LED led_51 (.in(programme_counter_1_ln[6]));
  LED led_52 (.in(programme_counter_1_ln[5]));
  LED led_53 (.in(programme_counter_1_ln[4]));
  Seven_Seg_Hex seven_seg_hex_15 (.d(flash_memory_1_q_adr_4), .dp(1'b0));
  LED led_54 (.in(flash_memory_1_q_adr_4[2]));
  LED led_55 (.in(flash_memory_1_q_adr_4[1]));
  LED led_56 (.in(flash_memory_1_q_adr_4[0]));
  PullDown pulldown_1 (.out(diodeforward_1_out));
  Button button_9 (.out(button_9_out));
  LED led_57 (.in(programme_counter_1_ln[2]));
  LED led_58 (.in(programme_counter_1_ln[3]));
  LED led_59 (.in(programme_counter_1_ln[1]));
  LED led_60 (.in(programme_counter_1_ln[0]));
  Seven_Seg_Hex seven_seg_hex_16 (.d(flash_memory_1_q_adr_3), .dp(1'b0));
  Seven_Seg_Hex seven_seg_hex_17 (.d(flash_memory_1_q_adr_2), .dp(1'b0));
  LED led_61 (.in(flash_memory_1_q_adr_3[2]));
  LED led_62 (.in(flash_memory_1_q_adr_3[3]));
  LED led_63 (.in(flash_memory_1_q_adr_3[1]));
  LED led_64 (.in(flash_memory_1_q_adr_3[0]));
  Programme_Counter programme_counter_1 (
    .DAT({flash_memory_1_q_dat_2, flash_memory_1_q_dat}),
    .ADR({flash_memory_1_q_adr_4, flash_memory_1_q_adr_3, flash_memory_1_q_adr_2, flash_memory_1_q_adr}),
    .CLK(or_1_out), .JMP(comparator_1_eq), .CJP(comparator_2_eq), .CLR(button_9_out),
    .LN({programme_counter_1_ln_3, programme_counter_1_ln_2, programme_counter_1_ln}));
  Flash_Memory flash_memory_1 (
    .LN({programme_counter_1_ln_3, programme_counter_1_ln_2, programme_counter_1_ln}),
    .DAT_dis(diodeforward_1_out), .ADR_dis(comparator_5_eq), .CLK(or_1_out),
    .Q_CMD({flash_memory_1_q_cmd_2, flash_memory_1_q_cmd}),
    .Q_DAT({flash_memory_1_q_dat_2, flash_memory_1_q_dat}),
    .Q_ADR({flash_memory_1_q_adr_4, flash_memory_1_q_adr_3, flash_memory_1_q_adr_2, flash_memory_1_q_adr}));
  // ALU alu_1: pin names not known; wires that end beside it: {flash_memory_1_q_cmd_2, flash_memory_1_q_cmd}, {flash_memory_1_q_dat_2, flash_memory_1_q_dat}, or_1_out, {flash_memory_1_q_dat_2, flash_memory_1_q_dat}, alu_1_p5, {alu_1_p6_2, alu_1_p6}, alu_1_p7
  DiodeForward diodeforward_7 (.in(alu_1_p5), .out(diodeforward_1_out));
  DAT_to_ADR_interface dat_to_adr_interface_1 (
    .DAT({flash_memory_1_q_dat_2, flash_memory_1_q_dat}), .STR_1(comparator_3_eq), .STR_2(comparator_4_eq),
    .LD(comparator_5_eq), .CLK(or_1_out),
    .ADR({flash_memory_1_q_adr_4, flash_memory_1_q_adr_3, flash_memory_1_q_adr_2, flash_memory_1_q_adr}));
  RAM ram_1 (
    .DAT({flash_memory_1_q_dat_2, flash_memory_1_q_dat}),
    .ADR({flash_memory_1_q_adr_4, flash_memory_1_q_adr_3, flash_memory_1_q_adr_2, flash_memory_1_q_adr}),
    .STR(comparator_6_eq), .LD(comparator_7_eq), .CLK(or_1_out),
    .Q({flash_memory_1_q_dat_2, flash_memory_1_q_dat}));
  Register register_1 (
    .D(dipswitch_3_out), .STR(or_2_out), .LD(comparator_9_eq), .CLK(or_1_out), .VAL(register_1_val),
    .Q({flash_memory_1_q_dat_2, flash_memory_1_q_dat}));
  Input_Control input_control_1 (
    .INP(button_8_out), .LD(comparator_10_eq), .CLK(or_1_out),
    .Q({flash_memory_1_q_dat_2, flash_memory_1_q_dat}));
  Register register_2 (
    .D({flash_memory_1_q_dat_2, flash_memory_1_q_dat}), .STR(comparator_11_eq), .LD(comparator_12_eq),
    .CLK(or_1_out), .VAL(register_2_val), .Q({flash_memory_1_q_dat_2, flash_memory_1_q_dat}));
  _8_By_8_Pixel_Display _8_by_8_pixel_display_1 (
    .DAT({flash_memory_1_q_dat_2, flash_memory_1_q_dat}),
    .ADR({flash_memory_1_q_adr_4, flash_memory_1_q_adr_3, flash_memory_1_q_adr_2, flash_memory_1_q_adr}),
    .STR(comparator_13_eq), .LD(comparator_14_eq), .CLK(or_1_out), .OUT(_8_by_8_pixel_display_1_out),
    .Q({flash_memory_1_q_dat_2, flash_memory_1_q_dat}));
  Controller_Input controller_input_1 (
    .IN(button_2_out), .LD(comparator_15_eq), .CLK(or_1_out),
    .Q({flash_memory_1_q_dat_2, flash_memory_1_q_dat}));
  Seven_Seg_Hex seven_seg_hex_18 (.d(flash_memory_1_q_adr), .dp(1'b0));
  LED led_65 (.in(flash_memory_1_q_adr_2[2]));
  LED led_66 (.in(flash_memory_1_q_adr_2[3]));
  LED led_67 (.in(flash_memory_1_q_adr_2[1]));
  LED led_68 (.in(flash_memory_1_q_adr_2[0]));
  LED led_69 (.in(flash_memory_1_q_adr[2]));
  LED led_70 (.in(flash_memory_1_q_adr[3]));
  LED led_71 (.in(flash_memory_1_q_adr[1]));
  LED led_72 (.in(flash_memory_1_q_adr[0]));
  LED led_73 (.in(_8_by_8_pixel_display_1_out[7]));
  LED led_74 (.in(_8_by_8_pixel_display_1_out[15]));
  LED led_75 (.in(_8_by_8_pixel_display_1_out[23]));
  LED led_76 (.in(_8_by_8_pixel_display_1_out[31]));
  LED led_77 (.in(_8_by_8_pixel_display_1_out[39]));
  LED led_78 (.in(_8_by_8_pixel_display_1_out[47]));
  LED led_79 (.in(_8_by_8_pixel_display_1_out[55]));
  LED led_80 (.in(_8_by_8_pixel_display_1_out[63]));
  Seven_Seg_Hex seven_seg_hex_19 (.d(register_2_val[7:4]), .dp(1'b0));
  LED led_81 (.in(register_2_val[6]));
  LED led_82 (.in(register_2_val[7]));
  LED led_83 (.in(_8_by_8_pixel_display_1_out[6]));
  LED led_84 (.in(_8_by_8_pixel_display_1_out[5]));
  LED led_85 (.in(_8_by_8_pixel_display_1_out[14]));
  LED led_86 (.in(_8_by_8_pixel_display_1_out[13]));
  LED led_87 (.in(_8_by_8_pixel_display_1_out[22]));
  LED led_88 (.in(_8_by_8_pixel_display_1_out[21]));
  LED led_89 (.in(_8_by_8_pixel_display_1_out[30]));
  LED led_90 (.in(_8_by_8_pixel_display_1_out[29]));
  LED led_91 (.in(_8_by_8_pixel_display_1_out[38]));
  LED led_92 (.in(_8_by_8_pixel_display_1_out[37]));
  LED led_93 (.in(_8_by_8_pixel_display_1_out[46]));
  LED led_94 (.in(_8_by_8_pixel_display_1_out[45]));
  LED led_95 (.in(_8_by_8_pixel_display_1_out[54]));
  LED led_96 (.in(_8_by_8_pixel_display_1_out[53]));
  LED led_97 (.in(_8_by_8_pixel_display_1_out[62]));
  LED led_98 (.in(_8_by_8_pixel_display_1_out[61]));
  Seven_Seg_Hex seven_seg_hex_20 (.d(register_2_val[3:0]), .dp(1'b0));
  LED led_99 (.in(register_2_val[5]));
  LED led_100 (.in(register_2_val[4]));
  LED led_101 (.in(register_2_val[3]));
  LED led_102 (.in(_8_by_8_pixel_display_1_out[4]));
  LED led_103 (.in(_8_by_8_pixel_display_1_out[3]));
  LED led_104 (.in(_8_by_8_pixel_display_1_out[12]));
  LED led_105 (.in(_8_by_8_pixel_display_1_out[11]));
  LED led_106 (.in(_8_by_8_pixel_display_1_out[20]));
  LED led_107 (.in(_8_by_8_pixel_display_1_out[19]));
  LED led_108 (.in(_8_by_8_pixel_display_1_out[28]));
  LED led_109 (.in(_8_by_8_pixel_display_1_out[27]));
  LED led_110 (.in(_8_by_8_pixel_display_1_out[36]));
  LED led_111 (.in(_8_by_8_pixel_display_1_out[35]));
  LED led_112 (.in(_8_by_8_pixel_display_1_out[44]));
  LED led_113 (.in(_8_by_8_pixel_display_1_out[43]));
  LED led_114 (.in(_8_by_8_pixel_display_1_out[52]));
  LED led_115 (.in(_8_by_8_pixel_display_1_out[51]));
  LED led_116 (.in(_8_by_8_pixel_display_1_out[60]));
  LED led_117 (.in(_8_by_8_pixel_display_1_out[59]));
  LED led_118 (.in(register_2_val[1]));
  LED led_119 (.in(register_2_val[0]));
  LED led_120 (.in(register_2_val[2]));
  LED led_121 (.in(_8_by_8_pixel_display_1_out[2]));
  LED led_122 (.in(_8_by_8_pixel_display_1_out[1]));
  LED led_123 (.in(_8_by_8_pixel_display_1_out[10]));
  LED led_124 (.in(_8_by_8_pixel_display_1_out[9]));
  LED led_125 (.in(_8_by_8_pixel_display_1_out[18]));
  LED led_126 (.in(_8_by_8_pixel_display_1_out[17]));
  LED led_127 (.in(_8_by_8_pixel_display_1_out[26]));
  LED led_128 (.in(_8_by_8_pixel_display_1_out[25]));
  LED led_129 (.in(_8_by_8_pixel_display_1_out[34]));
  LED led_130 (.in(_8_by_8_pixel_display_1_out[33]));
  LED led_131 (.in(_8_by_8_pixel_display_1_out[42]));
  LED led_132 (.in(_8_by_8_pixel_display_1_out[41]));
  LED led_133 (.in(_8_by_8_pixel_display_1_out[50]));
  LED led_134 (.in(_8_by_8_pixel_display_1_out[49]));
  LED led_135 (.in(_8_by_8_pixel_display_1_out[58]));
  LED led_136 (.in(_8_by_8_pixel_display_1_out[57]));
  LED led_137 (.in(_8_by_8_pixel_display_1_out[0]));
  LED led_138 (.in(_8_by_8_pixel_display_1_out[8]));
  LED led_139 (.in(_8_by_8_pixel_display_1_out[16]));
  LED led_140 (.in(_8_by_8_pixel_display_1_out[24]));
  LED led_141 (.in(_8_by_8_pixel_display_1_out[32]));
  LED led_142 (.in(_8_by_8_pixel_display_1_out[40]));
  LED led_143 (.in(_8_by_8_pixel_display_1_out[48]));
  LED led_144 (.in(_8_by_8_pixel_display_1_out[56]));

  // Notes on the sheet:
  //   clk_2: Hz: 500
  //   Input Buttons
  //   Clock Module
  //   Input Register
  //   T1
  //   A Reg
  //   B Reg
  //   T1--T0
  //   0        --      0          >          off
  //   0        --      1          >          button
  //   1        --      0          >          1hz
  //   1        --      1          >          max
  //   T0
  //   accept
  //   CMD
  //   Command
  //   DAT
  //   ADR
  //   CLK
  //   Programme Counter
  //   Data
  //   LN: current line of code being executed
  //   DAT_dis
  //   clear
  //   Address
  //   commands requiring the address bus to be disabled:
  //   Bus Transfer:
  //   - load from interface registers
  //   commands requiring the data bus to be disabled:
  //   Storage: 
  //   - load
  //   ALU:
  //   - add
  //   - add with carry
  //   - subtract
  //   incrementor:
  //   - increment
  //   - decrement
  //   logic:
  //   - binary not
  //   - binary or
  //   - binary and
  //   - binary xor
  //   - bitwise not
  //   - bitwise or
  //   - bitwise and
  //   - bitwise xor
  //   a/b/c registers:
  //   - load a
  //   - load b
  //   - load c
  //   compare:
  //   - bigger
  //   - equal
  //   - smaller
  //   flag reg:
  //   - load carry
  //   - load overflow
  //   - load flags
  //   Output Register
  //   Screen
endmodule
