// Digital circuit Command Decoder.dig as structural Verilog
module Command_Decoder (
  input  [7:0] IN,
  input  [7:0] CMP,
  output EN
);

  Comparator #(.Bits(8)) comparator_1 (.a(IN), .b(CMP), .eq(EN));  // open: gt, lt
endmodule
