// Digital circuit Comparator.dig as structural Verilog
module Comparator (
  input  [7:0] A,
  input  CMP_bigger,
  input  CMP_equal,
  input  CMP_smaller,
  input  [7:0] B,
  input  CLK,
  output [7:0] Q
);

  wire and_1_out, and_2_out, and_3_out, and_4_out, comparator_1_eq, comparator_1_gt, comparator_1_lt,
       d_ff_1_q, delay_1_out, not_1_out, or_1_out, or_2_out;
  wire [0:0] d_ff_2_q;

  Comparator #(.Bits(8)) comparator_1 (.a(A), .b(B), .gt(comparator_1_gt), .eq(comparator_1_eq), .lt(comparator_1_lt));
  not not_1 (not_1_out, CLK);
  or or_1 (or_1_out, CMP_bigger, CMP_equal, CMP_smaller);
  and and_1 (and_1_out, comparator_1_gt, CMP_bigger);
  and and_2 (and_2_out, comparator_1_eq, CMP_equal);
  and and_3 (and_3_out, comparator_1_lt, CMP_smaller);
  Delay delay_1 (.in(not_1_out), .out(delay_1_out));
  and and_4 (and_4_out, not_1_out, or_1_out);
  or or_2 (or_2_out, and_1_out, and_2_out, and_3_out);
  D_FF d_ff_1 (.D(and_4_out), .C(delay_1_out), .Q(d_ff_1_q));  // open: nQ
  D_FF d_ff_2 (.D(or_2_out), .C(d_ff_1_q), .Q(d_ff_2_q[0]));  // open: nQ
  assign Q = d_ff_1_q ? {{7{1'b0}}, d_ff_2_q[0]} : 8'bz;  // Driver driver_1

  // Notes on the sheet:
  //   would need the result to be output on the next falling edge 
  //   of the clock, where it stays until the falling edge after that.
  //   ->  for commands to able to use the result right after 
  //   the command as planned
  //   the delay could just be a few not gates
endmodule
