// Digital circuit Controller Input.dig as structural Verilog
module Controller_Input (
  input  [5:0] IN,
  input  LD,
  input  CLK,
  output [7:0] Q
);

  wire d_ff_1_q, not_1_out;
  wire [7:0] register_1_q;

  not not_1 (not_1_out, CLK);
  Register #(.Bits(8)) register_1 (.D({2'b00, IN}), .C(not_1_out), .en(1'b1), .Q(register_1_q));
  D_FF d_ff_1 (.D(LD), .C(not_1_out), .Q(d_ff_1_q));  // open: nQ
  assign Q = d_ff_1_q ? register_1_q : 8'bz;  // Driver driver_1

  // Notes on the sheet:
  //   D-Pad + Ok + Esc buttons ->
endmodule
