// Digital circuit DAT to ADR interface.dig as structural Verilog
module DAT_to_ADR_interface (
  input  [7:0] DAT,
  input  STR_1,
  input  STR_2,
  input  LD,
  input  CLK,
  output [15:0] ADR
);

  wire d_ff_1_q, d_ff_2_q, not_1_out;
  wire [7:0] register_1_q, register_2_q;

  not not_1 (not_1_out, CLK);
  Register #(.Bits(8)) register_1 (.D(DAT), .C(STR_1), .en(1'b1), .Q(register_1_q));
  Register #(.Bits(8)) register_2 (.D(DAT), .C(STR_2), .en(1'b1), .Q(register_2_q));
  D_FF d_ff_1 (.D(LD), .C(not_1_out), .Q(d_ff_1_q));  // open: nQ
  D_FF d_ff_2 (.D(d_ff_1_q), .C(not_1_out), .Q(d_ff_2_q));  // open: nQ
  assign ADR = d_ff_2_q ? {register_2_q, register_1_q} : 16'bz;  // Driver driver_1

  // Notes on the sheet:
  //   added another d latch for further delay
  //   otherwise this circuit would have
  //   no use
endmodule
