// Digital circuit Flag Register.dig as structural Verilog
module Flag_Register (
  input  [7:0] DAT,
  input  C_8,
  input  F,
  input  STC,
  input  STF,
  input  STA,
  input  LDC,
  input  LDF,
  input  LDA,
  input  CLK,
  output [7:0] Q,
  output C
);

  wire and_1_out, and_2_out, d_ff_2_q, d_ff_3_q, d_ff_4_q, d_ff_5_q, not_1_out, or_1_out, or_2_out, or_3_out,
       or_4_out, or_5_out, or_6_out, or_7_out;
  wire [1:0] and_3_out;

  or or_1 (or_1_out, DAT[0], C_8);
  or or_2 (or_2_out, DAT[1], F);
  or or_3 (or_3_out, STC, STA);
  or or_4 (or_4_out, STF, STA);
  not not_1 (not_1_out, CLK);
  and and_1 (and_1_out, not_1_out, or_3_out);
  and and_2 (and_2_out, not_1_out, or_4_out);
  or or_5 (or_5_out, LDC, LDA);
  or or_6 (or_6_out, LDF, LDA);
  or or_7 (or_7_out, LDC, LDF, LDA);
  D_FF d_ff_1 (.D(or_1_out), .C(and_1_out), .Q(C));  // open: nQ
  D_FF d_ff_2 (.D(or_2_out), .C(and_2_out), .Q(d_ff_2_q));  // open: nQ
  D_FF d_ff_3 (.D(or_5_out), .C(not_1_out), .Q(d_ff_3_q));  // open: nQ
  D_FF d_ff_4 (.D(or_6_out), .C(not_1_out), .Q(d_ff_4_q));  // open: nQ
  D_FF d_ff_5 (.D(or_7_out), .C(not_1_out), .Q(d_ff_5_q));  // open: nQ
  and and_3 (and_3_out[0], C, d_ff_3_q);
  and and_4 (and_3_out[1], d_ff_2_q, d_ff_4_q);
  assign Q = d_ff_5_q ? {{6{1'b0}}, and_3_out} : 8'bz;  // Driver driver_1

  // Notes on the sheet:
  //   DAT: connection to the data bus
  //   C_8: carry out from the adder
  //   F: oveflow from the subtractor
  //   STC: store carry
  //   STF: store overflow
  //   STA: store all from bus
  //   LDC: load carry
  //   LDF: load overflow
  //   LDA: load all
  //   CLK: clock input
  //   C_8 - carry out
  //   F - overflow
endmodule
