// Digital circuit Flash Memory.dig as structural Verilog
module Flash_Memory (
  input  [7:0] CMD,
  input  [7:0] DAT,
  input  [15:0] ADR,
  input  CLK,
  output [7:0] Q_CMD,
  output [7:0] Q_DAT,
  output [15:0] Q_ADR
);

  wire comparator_1_eq, comparator_2_eq, comparator_3_eq, comparator_4_eq, comparator_5_eq, comparator_6_eq,
       comparator_7_eq, comparator_8_eq, comparator_9_eq, comparator_10_eq, comparator_11_eq,
       comparator_12_eq, comparator_13_eq, comparator_14_eq, comparator_15_eq, comparator_16_eq,
       comparator_17_eq, comparator_18_eq, comparator_19_eq, comparator_20_eq, comparator_21_eq,
       comparator_22_eq, comparator_23_eq, comparator_24_eq, comparator_25_eq, comparator_26_eq, d_ff_1_q,
       d_ff_2_q, not_1_out, not_2_out, not_3_out, or_1_out, or_2_out, or_3_out, or_4_out, or_5_out, or_6_out,
       or_7_out;

  not not_1 (not_1_out, CLK);
  Comparator #(.Bits(8)) comparator_1 (.a(CMD), .b(8'h6), .eq(comparator_1_eq));  // open: gt, lt
  Comparator #(.Bits(8)) comparator_2 (.a(CMD), .b(8'hc), .eq(comparator_2_eq));  // open: gt, lt
  Comparator #(.Bits(8)) comparator_3 (.a(CMD), .b(8'hd), .eq(comparator_3_eq));  // open: gt, lt
  Comparator #(.Bits(8)) comparator_4 (.a(CMD), .b(8'he), .eq(comparator_4_eq));  // open: gt, lt
  Comparator #(.Bits(8)) comparator_5 (.a(CMD), .b(8'hf), .eq(comparator_5_eq));  // open: gt, lt
  or or_1 (or_1_out, comparator_1_eq, comparator_2_eq, comparator_3_eq, comparator_4_eq, comparator_5_eq);
  Comparator #(.Bits(8)) comparator_6 (.a(CMD), .b(8'h10), .eq(comparator_6_eq));  // open: gt, lt
  Comparator #(.Bits(8)) comparator_7 (.a(CMD), .b(8'h11), .eq(comparator_7_eq));  // open: gt, lt
  Comparator #(.Bits(8)) comparator_8 (.a(CMD), .b(8'h12), .eq(comparator_8_eq));  // open: gt, lt
  Comparator #(.Bits(8)) comparator_9 (.a(CMD), .b(8'h13), .eq(comparator_9_eq));  // open: gt, lt
  Comparator #(.Bits(8)) comparator_10 (.a(CMD), .b(8'h14), .eq(comparator_10_eq));  // open: gt, lt
  or or_2 (or_2_out, comparator_6_eq, comparator_7_eq, comparator_8_eq, comparator_9_eq, comparator_10_eq);
  Comparator #(.Bits(8)) comparator_11 (.a(CMD), .b(8'h15), .eq(comparator_11_eq));  // open: gt, lt
  Comparator #(.Bits(8)) comparator_12 (.a(CMD), .b(8'h16), .eq(comparator_12_eq));  // open: gt, lt
  Comparator #(.Bits(8)) comparator_13 (.a(CMD), .b(8'h17), .eq(comparator_13_eq));  // open: gt, lt
  Comparator #(.Bits(8)) comparator_14 (.a(CMD), .b(8'h18), .eq(comparator_14_eq));  // open: gt, lt
  Comparator #(.Bits(8)) comparator_15 (.a(CMD), .b(8'h19), .eq(comparator_15_eq));  // open: gt, lt
  or or_3 (or_3_out, comparator_11_eq, comparator_12_eq, comparator_13_eq, comparator_14_eq, comparator_15_eq);
  Comparator #(.Bits(8)) comparator_16 (.a(CMD), .b(8'h1a), .eq(comparator_16_eq));  // open: gt, lt
  Comparator #(.Bits(8)) comparator_17 (.a(CMD), .b(8'h1b), .eq(comparator_17_eq));  // open: gt, lt
  Comparator #(.Bits(8)) comparator_18 (.a(CMD), .b(8'h1d), .eq(comparator_18_eq));  // open: gt, lt
  Comparator #(.Bits(8)) comparator_19 (.a(CMD), .b(8'h1f), .eq(comparator_19_eq));  // open: gt, lt
  Comparator #(.Bits(8)) comparator_20 (.a(CMD), .b(8'h21), .eq(comparator_20_eq));  // open: gt, lt
  or or_4 (or_4_out, comparator_16_eq, comparator_17_eq, comparator_18_eq, comparator_19_eq, comparator_20_eq);
  Comparator #(.Bits(8)) comparator_21 (.a(CMD), .b(8'h23), .eq(comparator_21_eq));  // open: gt, lt
  Comparator #(.Bits(8)) comparator_22 (.a(CMD), .b(8'h24), .eq(comparator_22_eq));  // open: gt, lt
  Comparator #(.Bits(8)) comparator_23 (.a(CMD), .b(8'h25), .eq(comparator_23_eq));  // open: gt, lt
  or or_5 (or_5_out, comparator_21_eq, comparator_22_eq, comparator_23_eq);
  or or_6 (or_6_out, or_5_out, or_4_out, or_3_out, or_2_out, or_1_out);
  Comparator #(.Bits(8)) comparator_24 (.a(CMD), .b(8'h26), .eq(comparator_24_eq));  // open: gt, lt
  Comparator #(.Bits(8)) comparator_25 (.a(CMD), .b(8'h27), .eq(comparator_25_eq));  // open: gt, lt
  D_FF d_ff_1 (.D(or_6_out), .C(not_1_out), .Q(d_ff_1_q));  // open: nQ
  or or_7 (or_7_out, comparator_24_eq, comparator_25_eq, d_ff_1_q);
  Comparator #(.Bits(8)) comparator_26 (.a(CMD), .b(8'hb), .eq(comparator_26_eq));  // open: gt, lt
  not not_2 (not_2_out, or_7_out);
  not not_3 (not_3_out, comparator_26_eq);
  D_FF d_ff_2 (.D(not_3_out), .C(not_1_out), .Q(d_ff_2_q));  // open: nQ
  assign Q_DAT = not_2_out ? DAT : 8'bz;  // Driver driver_1
  assign Q_ADR = d_ff_2_q ? ADR : 16'bz;  // Driver driver_2

  assign Q_CMD = CMD;

  // Notes on the sheet:
  //   extended bus disable
  //   single tick bus disable
  //   extended address bus disable
  //   commands where a bus needs to be disabled for 1 cycle:
  //   shift register:
  //   - shift
  //   - shift circular
  //   commands where a bus needs to be disabled for 2 cycles:
  //   Storage: 
  //   - load > data
  //   - load to address bus > address
  //   ALU:
  //   - add > data
  //   - add with carry > data
  //   - subtract > data
  //   incrementor:
  //   - increment > data
  //   - decrement > data
  //   logic:
  //   - binary not
  //   - binary or
  //   - binary and
  //   - binary xor
  //   - bitwise not
  //   - bitwise or
  //   - bitwise and
  //   - bitwise xor
  //   a/b/c registers:
  //   - load a > data
  //   - load b > data
  //   - load c > data
  //   compare:
  //   - bigger > data
  //   - equal > data
  //   - smaller > data
  //   flag reg:
  //   - load carry > data
  //   - load overflow > data
  //   - load flags > data
endmodule
