// Digital circuit Programme Counter.dig as structural Verilog
module Programme_Counter (
  input  [7:0] DAT,
  input  CLK,
  input  STJ_1,
  input  STJ_2,
  input  JMP,
  input  CJP,
  input  CLR,
  output [15:0] LN
);

  wire _8_input_or_1_p2, and_1_out, or_1_out;
  wire [7:0] register_1_q, register_2_q;

  // _8_Input_Or _8_input_or_1: pin names not known; wires that end beside it: DAT, _8_input_or_1_p2
  Register #(.Bits(8)) register_1 (.D(DAT), .C(STJ_1), .en(1'b1), .Q(register_1_q));
  Register #(.Bits(8)) register_2 (.D(DAT), .C(STJ_2), .en(1'b1), .Q(register_2_q));
  and and_1 (and_1_out, _8_input_or_1_p2, CJP);
  or or_1 (or_1_out, JMP, and_1_out);
  CounterPreset #(.maxValue(65535), .Bits(16), .isProgramCounter("true")) counterpreset_1 (
    .en(1'b1), .C(CLK), .dir(1'b0), .in({register_2_q, register_1_q}), .ld(or_1_out), .clr(CLR), .out(LN));  // open: ovf

  // Notes on the sheet:
  //   DAT: Data input
  //   CLK: Clock input
  //   STJ1: Store to jump reg 1
  //   STJ2: Store to jump reg 2
  //   JMP: Jump command
  //   CJP: Conditional Jump command
  //   CLR: Clear for starting the CPU
endmodule
