// Digital circuit RAM.dig as structural Verilog
module RAM (
  input  [7:0] DAT,
  input  [15:0] ADR,
  input  STR_reg1,
  input  STR_reg2,
  input  STR,
  input  LD,
  input  STR_todata,
  input  LD_fromdata,
  input  LD_reg1,
  input  LD_reg2,
  input  LD_toaddrbus,
  input  CLK,
  output [7:0] Q_DAT,
  output [15:0] Q_ADR
);

  wire d_ff_1_q, d_ff_2_q, d_ff_3_q, delay_1_out, delay_2_out, not_1_out, not_2_out, or_1_out, or_2_out,
       or_3_out, or_4_out;
  wire [7:0] ramdualport_1_d, register_1_q, register_2_q, register_3_q, register_4_q;
  wire [15:0] driver_1_out, driver_2_out, or_5_out;

  not not_1 (not_1_out, CLK);
  Delay delay_1 (.in(STR_reg1), .out(delay_1_out));
  Delay delay_2 (.in(STR_reg2), .out(delay_2_out));
  D_FF d_ff_1 (.D(LD), .C(not_1_out), .Q(d_ff_1_q));  // open: nQ
  D_FF d_ff_2 (.D(LD_fromdata), .C(not_1_out), .Q(d_ff_2_q));  // open: nQ
  D_FF d_ff_3 (.D(LD_toaddrbus), .C(not_1_out), .Q(d_ff_3_q));  // open: nQ
  Register #(.Bits(8)) register_1 (.D(DAT), .C(delay_1_out), .en(1'b1), .Q(register_1_q));
  Register #(.Bits(8)) register_2 (.D(DAT), .C(delay_2_out), .en(1'b1), .Q(register_2_q));
  or or_1 (or_1_out, STR_todata, d_ff_2_q);
  or or_2 (or_2_out, STR_todata, STR);
  or or_3 (or_3_out, d_ff_2_q, d_ff_1_q, d_ff_3_q);
  or or_4 (or_4_out, d_ff_2_q, d_ff_1_q);
  assign driver_1_out = or_1_out ? {register_2_q, register_1_q} : 16'bz;  // Driver driver_1
  assign driver_2_out = not_2_out ? ADR : 16'bz;  // Driver driver_2
  assign or_5_out = driver_2_out | driver_1_out;  // Or or_5, 16 bits wide
  not not_2 (not_2_out, or_1_out);
  RAMDualPort #(.AddrBits(16), .Bits(8)) ramdualport_1 (
    .A(or_5_out), .Din(DAT), .str(or_2_out), .C(not_1_out), .ld(or_3_out), .D(ramdualport_1_d));
  Register #(.Bits(8)) register_3 (.D(ramdualport_1_d), .C(LD_reg1), .en(1'b1), .Q(register_3_q));
  Register #(.Bits(8)) register_4 (.D(ramdualport_1_d), .C(LD_reg2), .en(1'b1), .Q(register_4_q));
  assign Q_ADR = d_ff_3_q ? {register_4_q, register_3_q} : 16'bz;  // Driver driver_3
  assign Q_DAT = or_4_out ? ramdualport_1_d : 8'bz;  // Driver driver_4

  // Notes on the sheet:
  //   two subsequent load commands can't be performed,
  //   since the previous address stays buffered.
  //   not a problem, just an observation
  //   (since the data after a load command just persists for
  //   one clock pulse, the first operation would be redundant)
  //   str - store to ram
  //   ld - write to data bus
  //    (output enable)
  //   could be a 
  //   few AND gates
endmodule
