// Digital circuit Register.dig as structural Verilog
module Register (
  input  [7:0] D,
  input  STR,
  input  LD,
  input  CLK,
  output [7:0] VAL,
  output [7:0] Q
);

  wire and_1_out, d_ff_1_q, delay_1_out, not_1_out, rising_edge_detector_1_q;

  not not_1 (not_1_out, CLK);
  Delay delay_1 (.in(CLK), .out(delay_1_out));
  D_FF d_ff_1 (.D(LD), .C(not_1_out), .Q(d_ff_1_q));  // open: nQ
  Rising_Edge_Detector rising_edge_detector_1 (.D(delay_1_out), .Q(rising_edge_detector_1_q));
  and and_1 (and_1_out, STR, rising_edge_detector_1_q);
  Register #(.Bits(8)) register_1 (.D(D), .C(and_1_out), .en(1'b1), .Q(VAL));
  assign Q = d_ff_1_q ? VAL : 8'bz;  // Driver driver_1

  // Notes on the sheet:
  //   !!!!!!!!!!!! not needed in the final design !!!!!!!
  //   The signal to the store input on the register needs
  //   to be long enough for the register to store the value
  //   as specified in the datasheet of whatever register we 
  //   end up using.
  //   The delay used here should be long enough for the 
  //   STR command to arrive right before the rising edge of
  //   CLK, and it should be long enough for the STR command
  //   to be gone the next cycle, before the rising edge comes,
  //   so that there is no accidental storing done during
  //   the next cycle.
endmodule
