// Digital circuit Rising Edge Detector.dig as structural Verilog
module Rising_Edge_Detector (
  input  D,
  output Q
);

  wire delay_1_out;

  Delay delay_1 (.in(D), .out(delay_1_out));
  and and_1 (Q, ~delay_1_out, D);  // And
endmodule
