// Digital circuit Shift Register.dig as structural Verilog
module Shift_Register (
  input  [7:0] A,
  input  [7:0] Dis,
  input  Cir,
  output [7:0] Q
);

  wire and_1_out, and_2_out, and_3_out, and_4_out, and_5_out, and_6_out, and_7_out, multiplexer_1_out,
       multiplexer_2_out, multiplexer_3_out, multiplexer_4_out, multiplexer_5_out, multiplexer_6_out,
       multiplexer_7_out, multiplexer_8_out, multiplexer_9_out, multiplexer_10_out, multiplexer_11_out,
       multiplexer_12_out, multiplexer_13_out, multiplexer_14_out, multiplexer_15_out, multiplexer_16_out;

  and and_1 (and_1_out, A[0], Cir);
  Multiplexer multiplexer_1 (.sel(Dis[0]), .in_0(A[0]), .in_1(A[1]), .out(multiplexer_1_out));
  Multiplexer multiplexer_2 (.sel(Dis[0]), .in_0(A[1]), .in_1(A[2]), .out(multiplexer_2_out));
  Multiplexer multiplexer_3 (.sel(Dis[0]), .in_0(A[2]), .in_1(A[3]), .out(multiplexer_3_out));
  Multiplexer multiplexer_4 (.sel(Dis[0]), .in_0(A[3]), .in_1(A[4]), .out(multiplexer_4_out));
  Multiplexer multiplexer_5 (.sel(Dis[0]), .in_0(A[4]), .in_1(A[5]), .out(multiplexer_5_out));
  Multiplexer multiplexer_6 (.sel(Dis[0]), .in_0(A[5]), .in_1(A[6]), .out(multiplexer_6_out));
  Multiplexer multiplexer_7 (.sel(Dis[0]), .in_0(A[6]), .in_1(A[7]), .out(multiplexer_7_out));
  Multiplexer multiplexer_8 (.sel(Dis[0]), .in_0(A[7]), .in_1(and_1_out), .out(multiplexer_8_out));
  and and_2 (and_2_out, multiplexer_1_out, Cir);
  and and_3 (and_3_out, multiplexer_2_out, Cir);
  Multiplexer multiplexer_9 (.sel(Dis[1]), .in_0(multiplexer_1_out), .in_1(multiplexer_3_out), .out(multiplexer_9_out));
  Multiplexer multiplexer_10 (
    .sel(Dis[1]), .in_0(multiplexer_2_out), .in_1(multiplexer_4_out), .out(multiplexer_10_out));
  Multiplexer multiplexer_11 (
    .sel(Dis[1]), .in_0(multiplexer_3_out), .in_1(multiplexer_5_out), .out(multiplexer_11_out));
  Multiplexer multiplexer_12 (
    .sel(Dis[1]), .in_0(multiplexer_4_out), .in_1(multiplexer_6_out), .out(multiplexer_12_out));
  Multiplexer multiplexer_13 (
    .sel(Dis[1]), .in_0(multiplexer_5_out), .in_1(multiplexer_7_out), .out(multiplexer_13_out));
  Multiplexer multiplexer_14 (
    .sel(Dis[1]), .in_0(multiplexer_6_out), .in_1(multiplexer_8_out), .out(multiplexer_14_out));
  Multiplexer multiplexer_15 (.sel(Dis[1]), .in_0(multiplexer_7_out), .in_1(and_2_out), .out(multiplexer_15_out));
  Multiplexer multiplexer_16 (.sel(Dis[1]), .in_0(multiplexer_8_out), .in_1(and_3_out), .out(multiplexer_16_out));
  and and_4 (and_4_out, multiplexer_9_out, Cir);
  and and_5 (and_5_out, multiplexer_10_out, Cir);
  and and_6 (and_6_out, multiplexer_11_out, Cir);
  and and_7 (and_7_out, multiplexer_12_out, Cir);
  Multiplexer multiplexer_17 (.sel(Dis[2]), .in_0(multiplexer_9_out), .in_1(multiplexer_13_out), .out(Q[0]));
  Multiplexer multiplexer_18 (.sel(Dis[2]), .in_0(multiplexer_10_out), .in_1(multiplexer_14_out), .out(Q[1]));
  Multiplexer multiplexer_19 (.sel(Dis[2]), .in_0(multiplexer_11_out), .in_1(multiplexer_15_out), .out(Q[2]));
  Multiplexer multiplexer_20 (.sel(Dis[2]), .in_0(multiplexer_12_out), .in_1(multiplexer_16_out), .out(Q[3]));
  Multiplexer multiplexer_21 (.sel(Dis[2]), .in_0(multiplexer_13_out), .in_1(and_4_out), .out(Q[4]));
  Multiplexer multiplexer_22 (.sel(Dis[2]), .in_0(multiplexer_14_out), .in_1(and_5_out), .out(Q[5]));
  Multiplexer multiplexer_23 (.sel(Dis[2]), .in_0(multiplexer_15_out), .in_1(and_6_out), .out(Q[6]));
  Multiplexer multiplexer_24 (.sel(Dis[2]), .in_0(multiplexer_16_out), .in_1(and_7_out), .out(Q[7]));

  // Notes on the sheet:
  //   Dis: The distance that A should be shifted by
  //   Cir: If the operation should be circular
endmodule
