// Digital circuit 8Bit ALU.dig as structural Verilog
module _8Bit_ALU (
  input  [7:0] CMD,
  input  [7:0] DAT,
  input  CLK
);

  // _8Bit_Reg _8bit_reg_1: pin names not known
  // _8Bit_Reg _8bit_reg_2: pin names not known; wires that end beside it: 8'h1
  CMD_DEC cmd_dec_1 ();  // open: CMD_IN, CMD_CMP, CMD_EN
  ALU_CMD_Decoder alu_cmd_decoder_1 ();  // open: CMD, LDA, CLA, LDB, CLB, ADD, SUB, INC, TOF, CMP, NOT, OR, XOR, AND, SHL, SHR, SLD, LDF
  // Flag_Register flag_register_1: pin names not known
  // _8Bit_Adder _8bit_adder_1: pin names not known
  // _8Bit_Comparator _8bit_comparator_1: pin names not known
  // _8Bit_Logic_Operations _8bit_logic_operations_1: pin names not known
  _8Bit_Shift_Register _8bit_shift_register_1 ();  // open: Q, A, CLK, nR, S0, S1
endmodule
