// Digital circuit 8Bit Reg.dig as structural Verilog
module _8Bit_Reg (
  input  [7:0] In,
  input  nR,
  input  LD,
  output [7:0] Q
);

  _74273 _74273_1 (
    .pin1(nR), .pin2(Q[0]), .pin3(In[0]), .pin4(In[1]), .pin5(Q[1]), .pin6(Q[2]), .pin7(In[2]), .pin8(In[3]),
    .pin9(Q[3]), .pin10(1'b0), .pin11(LD), .pin12(Q[4]), .pin13(In[4]), .pin14(In[5]), .pin15(Q[5]),
    .pin16(Q[6]), .pin17(In[6]), .pin18(In[7]), .pin19(Q[7]), .pin20(1'b1));
endmodule
