// Digital circuit 74183.dig as structural Verilog
// 2 1bit full adders
module _74183 (
  input  _2B,
  input  _2Cn,
  input  _2A,
  input  _1Cn,
  input  _1A,
  input  _1B,
  input  VCC,
  input  GND,
  output _1Z,
  output _2Z,
  output _1Cn_plus_1,
  output _2Cn_plus_1
);

  Add add_1 (.a(_1Cn), .b(_1A), .c_i(_1B), .s(_1Z), .c_o(_1Cn_plus_1));
  Add add_2 (.a(_2Cn), .b(_2A), .c_i(_2B), .s(_2Z), .c_o(_2Cn_plus_1));
  PowerSupply powersupply_1 (.VDD(VCC), .GND(GND));

  // Notes on the sheet:
  //   _2B: pin 12
  //   _2Cn: pin 11
  //   _1Z: pin 6
  //   _2A: pin 13
  //   _2Z: pin 8
  //   _1Cn_plus_1: pin 5
  //   _1Cn: pin 4
  //   _1A: pin 1
  //   _1B: pin 3
  //   _2Cn_plus_1: pin 10
  //   VCC: pin 14, default 1
  //   GND: pin 7
endmodule

/* Test case:
# A complete test of all 512 possible additions
#

C0   A4 A3 A2 A1   B4 B3 B2 B1  C4 S4 S3 S2 S1
loop(A,16)
  loop(B,16)
0    bits(4,A)     bits(4,B)    bits(5,A+B)
1    bits(4,A)     bits(4,B)    bits(5,A+B+1)
  end loop
end loop
*/
