// Digital circuit 8Bit enable circuit.dig as structural Verilog
module _8Bit_enable_circuit (
  input  [7:0] In,
  input  En,
  output [7:0] Out
);

  D_FF d_ff_1 (.D(In[0]), .C(En), .Q(Out[0]));  // open: nQ
  D_FF d_ff_2 (.D(In[1]), .C(En), .Q(Out[1]));  // open: nQ
  D_FF d_ff_3 (.D(In[2]), .C(En), .Q(Out[2]));  // open: nQ
  D_FF d_ff_4 (.D(In[3]), .C(En), .Q(Out[3]));  // open: nQ
  D_FF d_ff_5 (.D(In[4]), .C(En), .Q(Out[4]));  // open: nQ
  D_FF d_ff_6 (.D(In[5]), .C(En), .Q(Out[5]));  // open: nQ
  D_FF d_ff_7 (.D(In[6]), .C(En), .Q(Out[6]));  // open: nQ
  D_FF d_ff_8 (.D(In[7]), .C(En), .Q(Out[7]));  // open: nQ
endmodule
