// Digital circuit 8Bit Adder.dig as structural Verilog
module _8Bit_Adder (
  input  Bit0,
  input  Bit1,
  input  Bit2,
  input  Bit3,
  input  Bit4,
  input  Bit5,
  input  Bit6,
  input  Bit7,
  input  Bit8,
  input  Bit9,
  input  Bit10,
  input  Bit11,
  input  Bit12,
  input  Bit13,
  input  Bit14,
  input  Bit15,
  input  Add_Sub,
  output Out7,
  output Out6,
  output Out5,
  output Out4,
  output Out3,
  output Out2,
  output Out1,
  output Out0,
  output Overflow
);

  wire and_1_out, and_2_out, and_3_out, and_4_out, and_5_out, and_6_out, and_7_out, and_8_out, and_9_out,
       and_10_out, and_11_out, and_12_out, and_13_out, and_14_out, and_15_out, and_16_out, or_1_out,
       or_2_out, or_3_out, or_4_out, or_5_out, or_6_out, or_7_out, or_8_out, xor_1_out, xor_2_out, xor_3_out,
       xor_4_out, xor_5_out, xor_6_out, xor_7_out, xor_8_out, xor_9_out, xor_10_out, xor_11_out, xor_12_out,
       xor_13_out, xor_14_out, xor_15_out, xor_16_out;

  xor xor_1 (xor_1_out, Bit13, Add_Sub);
  xor xor_2 (xor_2_out, Bit14, Add_Sub);
  xor xor_3 (xor_3_out, Bit15, Add_Sub);
  xor xor_4 (xor_4_out, Bit9, Add_Sub);
  xor xor_5 (xor_5_out, Bit10, Add_Sub);
  xor xor_6 (xor_6_out, Bit11, Add_Sub);
  xor xor_7 (xor_7_out, Bit12, Add_Sub);
  xor xor_8 (xor_8_out, Bit8, Add_Sub);
  xor xor_9 (xor_9_out, Add_Sub, Bit0);
  xor xor_10 (xor_10_out, or_1_out, Bit1);
  xor xor_11 (xor_11_out, or_2_out, Bit2);
  xor xor_12 (xor_12_out, or_3_out, Bit3);
  xor xor_13 (xor_13_out, or_4_out, Bit4);
  xor xor_14 (xor_14_out, or_5_out, Bit5);
  xor xor_15 (xor_15_out, or_6_out, Bit6);
  xor xor_16 (xor_16_out, or_7_out, Bit7);
  xor xor_17 (Out0, xor_9_out, xor_8_out);
  and and_1 (and_1_out, xor_9_out, xor_8_out);
  and and_2 (and_2_out, Bit0, Add_Sub);
  xor xor_18 (Out1, xor_10_out, xor_4_out);
  and and_3 (and_3_out, xor_10_out, xor_4_out);
  and and_4 (and_4_out, Bit1, or_1_out);
  xor xor_19 (Out2, xor_11_out, xor_5_out);
  and and_5 (and_5_out, xor_11_out, xor_5_out);
  and and_6 (and_6_out, Bit2, or_2_out);
  xor xor_20 (Out3, xor_12_out, xor_6_out);
  and and_7 (and_7_out, xor_12_out, xor_6_out);
  and and_8 (and_8_out, Bit3, or_3_out);
  xor xor_21 (Out4, xor_13_out, xor_7_out);
  and and_9 (and_9_out, xor_13_out, xor_7_out);
  and and_10 (and_10_out, Bit4, or_4_out);
  xor xor_22 (Out5, xor_14_out, xor_1_out);
  and and_11 (and_11_out, xor_14_out, xor_1_out);
  and and_12 (and_12_out, Bit5, or_5_out);
  xor xor_23 (Out6, xor_15_out, xor_2_out);
  and and_13 (and_13_out, xor_15_out, xor_2_out);
  and and_14 (and_14_out, Bit6, or_6_out);
  xor xor_24 (Out7, xor_16_out, xor_3_out);
  and and_15 (and_15_out, xor_16_out, xor_3_out);
  and and_16 (and_16_out, Bit7, or_7_out);
  or or_1 (or_1_out, and_1_out, and_2_out);
  or or_2 (or_2_out, and_3_out, and_4_out);
  or or_3 (or_3_out, and_5_out, and_6_out);
  or or_4 (or_4_out, and_7_out, and_8_out);
  or or_5 (or_5_out, and_9_out, and_10_out);
  or or_6 (or_6_out, and_11_out, and_12_out);
  or or_7 (or_7_out, and_13_out, and_14_out);
  or or_8 (or_8_out, and_15_out, and_16_out);
  xor xor_25 (Overflow, or_8_out, or_7_out);
endmodule
