// Digital circuit 8Bit Register with Clear.dig as structural Verilog
module _8Bit_Register_with_Clear (
  input  Bit_0,
  input  Bit_1,
  input  Bit_2,
  input  Bit_3,
  input  Bit_4,
  input  Bit_5,
  input  Bit_6,
  input  Bit_7,
  input  CLR,
  input  CLK,
  output Out_0,
  output Out_1,
  output Out_2,
  output Out_3,
  output Out_4,
  output Out_5,
  output Out_6,
  output Out_7
);

  wire and_1_out, and_2_out, and_3_out, and_4_out, and_5_out, and_6_out, and_7_out, and_8_out, and_9_out,
       and_10_out, and_11_out, and_12_out, and_13_out, and_14_out, and_15_out, and_16_out, and_17_out,
       or_1_out, or_2_out, or_3_out, or_4_out, or_5_out, or_6_out, or_7_out, or_8_out, rs_ff_as_1_nq,
       rs_ff_as_2_nq, rs_ff_as_3_nq, rs_ff_as_4_nq, rs_ff_as_5_nq, rs_ff_as_6_nq, rs_ff_as_7_nq,
       rs_ff_as_8_nq;

  and and_1 (and_1_out, ~CLK, CLR);  // And
  and and_2 (and_2_out, rs_ff_as_1_nq, CLK, Bit_0);
  and and_3 (and_3_out, ~Bit_0, CLK, Out_0);  // And
  and and_4 (and_4_out, rs_ff_as_2_nq, CLK, Bit_1);
  and and_5 (and_5_out, ~Bit_1, CLK, Out_1);  // And
  and and_6 (and_6_out, rs_ff_as_3_nq, CLK, Bit_2);
  and and_7 (and_7_out, ~Bit_2, CLK, Out_2);  // And
  and and_8 (and_8_out, rs_ff_as_4_nq, CLK, Bit_3);
  and and_9 (and_9_out, ~Bit_3, CLK, Out_3);  // And
  and and_10 (and_10_out, rs_ff_as_5_nq, CLK, Bit_4);
  and and_11 (and_11_out, ~Bit_4, CLK, Out_4);  // And
  and and_12 (and_12_out, rs_ff_as_6_nq, CLK, Bit_5);
  and and_13 (and_13_out, ~Bit_5, CLK, Out_5);  // And
  and and_14 (and_14_out, rs_ff_as_7_nq, CLK, Bit_6);
  and and_15 (and_15_out, ~Bit_6, CLK, Out_6);  // And
  and and_16 (and_16_out, rs_ff_as_8_nq, CLK, Bit_7);
  and and_17 (and_17_out, ~Bit_7, CLK, Out_7);  // And
  or or_1 (or_1_out, and_3_out, and_1_out);
  or or_2 (or_2_out, and_5_out, and_1_out);
  or or_3 (or_3_out, and_7_out, and_1_out);
  or or_4 (or_4_out, and_9_out, and_1_out);
  or or_5 (or_5_out, and_11_out, and_1_out);
  or or_6 (or_6_out, and_13_out, and_1_out);
  or or_7 (or_7_out, and_15_out, and_1_out);
  or or_8 (or_8_out, and_17_out, and_1_out);
  RS_FF_AS rs_ff_as_1 (.S(and_2_out), .R(or_1_out), .Q(Out_0), .nQ(rs_ff_as_1_nq));
  RS_FF_AS rs_ff_as_2 (.S(and_4_out), .R(or_2_out), .Q(Out_1), .nQ(rs_ff_as_2_nq));
  RS_FF_AS rs_ff_as_3 (.S(and_6_out), .R(or_3_out), .Q(Out_2), .nQ(rs_ff_as_3_nq));
  RS_FF_AS rs_ff_as_4 (.S(and_8_out), .R(or_4_out), .Q(Out_3), .nQ(rs_ff_as_4_nq));
  RS_FF_AS rs_ff_as_5 (.S(and_10_out), .R(or_5_out), .Q(Out_4), .nQ(rs_ff_as_5_nq));
  RS_FF_AS rs_ff_as_6 (.S(and_12_out), .R(or_6_out), .Q(Out_5), .nQ(rs_ff_as_6_nq));
  RS_FF_AS rs_ff_as_7 (.S(and_14_out), .R(or_7_out), .Q(Out_6), .nQ(rs_ff_as_7_nq));
  RS_FF_AS rs_ff_as_8 (.S(and_16_out), .R(or_8_out), .Q(Out_7), .nQ(rs_ff_as_8_nq));
endmodule
